// Logisim project Project3Final.circ as structural Verilog: 12 circuits, main circuit CPU15
module main (
  input  EnableBreakpoint,
  input  [14:0] Breakpoint
);

  wire and_2_out, and_3_out, chipset_1_irq, CLK, clock_1_out, cpu15_1_c, cpu15_1_e, cpu15_1_n, cpu15_1_o,
       cpu15_1_z, KBCLR, KBIRQ, KBRD, MEMCS, nand_1_out, RE, TTYCLR, TTYWE, undriven, WE;
  wire [6:0] KBDATA, TTYDATA;
  wire [7:0] cpu15_1_srf;
  wire [14:0] ADDR, chipset_1_ivect, chipset_1_led0, chipset_1_led1, chipset_1_led2, chipset_1_led3,
       chipset_1_led4, chipset_1_led5, chipset_1_led6, chipset_1_led7, chipset_1_led8, chipset_1_led9,
       chipset_1_leda, chipset_1_ledb, chipset_1_ledc, chipset_1_ledd, chipset_1_lede, cpu15_1_ib,
       cpu15_1_pc, cpu15_1_r0, cpu15_1_r1, cpu15_1_r2, cpu15_1_r3, cpu15_1_r4, cpu15_1_r5, cpu15_1_r6,
       cpu15_1_r7, cpu15_1_srp, DATA, xnor_1_out;

  Clock clock_1 (.out(clock_1_out));
  nand nand_1 (nand_1_out, EnableBreakpoint, xnor_1_out[0], xnor_1_out[1], xnor_1_out[2], xnor_1_out[3], xnor_1_out[4], xnor_1_out[5], xnor_1_out[6], xnor_1_out[7], xnor_1_out[8], xnor_1_out[9], xnor_1_out[10], xnor_1_out[11], xnor_1_out[12], xnor_1_out[13], xnor_1_out[14], 1'b1);
  and and_1 (CLK, clock_1_out, nand_1_out);
  assign xnor_1_out = ~(Breakpoint ^ cpu15_1_pc);  // XNOR_Gate xnor_1, 15 bits wide
  LED I (.in(cpu15_1_z));
  LED Z (.in(cpu15_1_n));
  LED N (.in(cpu15_1_o));
  LED O (.in(cpu15_1_c));
  LED C (.in(cpu15_1_e));
  LED E (.in(undriven));
  and and_2 (and_2_out, WE, MEMCS);
  and and_3 (and_3_out, MEMCS, RE);
  RAM #(.addrWidth(15), .asyncread("true"), .dataWidth(15), .databus("bidir")) ram_1 (
    .addr(ADDR), .we(and_2_out), .oe(and_3_out), .clk(CLK), .data(DATA));
  // Probe on cpu15_1_pc
  // Probe on cpu15_1_ib
  // Probe on cpu15_1_srp
  // Probe on cpu15_1_srf
  // Probe on cpu15_1_r0
  // Probe on cpu15_1_r1
  // Probe on cpu15_1_r2
  // Probe on cpu15_1_r3
  // Probe on cpu15_1_r4
  // Probe on cpu15_1_r5
  // Probe on cpu15_1_r6
  // Probe on cpu15_1_r7
  CPU15 cpu15_1 (
    .Z(cpu15_1_z), .N(cpu15_1_n), .O(cpu15_1_o), .C(cpu15_1_c), .E(cpu15_1_e), .in_2(undriven),
    .PC(cpu15_1_pc), .IB(cpu15_1_ib), .SRP(cpu15_1_srp), .SRF(cpu15_1_srf), .R0(cpu15_1_r0), .R1(cpu15_1_r1),
    .R2(cpu15_1_r2), .R3(cpu15_1_r3), .R4(cpu15_1_r4), .R5(cpu15_1_r5), .R6(cpu15_1_r6), .R7(cpu15_1_r7),
    .CLK(CLK), .IRQ(chipset_1_irq), .RE(RE), .WE(WE), .ADDR(ADDR), .DATAIN(DATA), .DATAOUT(DATA));  // open: I
  // Probe on ADDR
  // Probe on DATA
  // Probe on chipset_1_ivect
  // Probe on TTYDATA
  CHIPSET chipset_1 (
    .RE(RE), .WE(WE), .ADDR(ADDR), .CPUDATAIN(DATA), .CPUDATAOUT(DATA), .IRQ(chipset_1_irq),
    .IVECT(chipset_1_ivect), .CLK(CLK), .MEMCS(MEMCS), .TTYWR(TTYWE), .TTYCLR(TTYCLR), .TTYDATA(TTYDATA),
    .KBRD(KBRD), .KBCLR(KBCLR), .KBIRQ(KBIRQ), .KBDATA(KBDATA), .LED0(chipset_1_led0), .LED1(chipset_1_led1),
    .LED2(chipset_1_led2), .LED3(chipset_1_led3), .LED4(chipset_1_led4), .LED5(chipset_1_led5),
    .LED6(chipset_1_led6), .LED7(chipset_1_led7), .LED8(chipset_1_led8), .LED9(chipset_1_led9),
    .LEDA(chipset_1_leda), .LEDB(chipset_1_ledb), .LEDC(chipset_1_ledc), .LEDD(chipset_1_ledd),
    .LEDE(chipset_1_lede));
  TTY tty_1 (.data(TTYDATA), .clk(CLK), .we(TTYWE), .clr(TTYCLR));
  Keyboard keyboard_1 (.clk(CLK), .re(KBRD), .clr(KBCLR), .avail(KBIRQ), .data(KBDATA));
  DotMatrix #(.matrixcols(15), .matrixrows(15)) dotmatrix_1 (
    .col0(chipset_1_led0), .col1(chipset_1_led1), .col2(chipset_1_led2), .col3(chipset_1_led3),
    .col4(chipset_1_led4), .col5(chipset_1_led5), .col6(chipset_1_led6), .col7(chipset_1_led7),
    .col8(chipset_1_led8), .col9(chipset_1_led9), .col10(chipset_1_leda), .col11(chipset_1_ledb),
    .col12(chipset_1_ledc), .col13(chipset_1_ledd), .col14(chipset_1_lede));
endmodule

// CPU
module CPU15 (
  input  [14:0] DATAIN,
  input  in_2,
  input  CLK,
  input  IRQ,
  output [14:0] PC,
  output [14:0] IB,
  output [14:0] SRP,
  output [7:0] SRF,
  output [14:0] R0,
  output [14:0] R1,
  output [14:0] R2,
  output [14:0] R3,
  output [14:0] R4,
  output [14:0] R5,
  output [14:0] R6,
  output [14:0] R7,
  output RE,
  output WE,
  output I,
  output Z,
  output [14:0] ADDR,
  output N,
  output O,
  output C,
  output E,
  output [14:0] DATAOUT
);

  wire and_1_out, and_10_out, BCF, BJump, BJumpEN, BJumpPC_UPDATE, BNCF, BNF, BNNF, BNZF, BZF, DATA_SELECT,
       decoder_1_out0, decoder_1_out1, decoder_1_out2, decoder_1_out3, decoder_1_out4, decoder_1_out5,
       decoder_1_out6, decoder_1_out7, decoder_1_out8, decoder_1_out10, decoder_1_out11, decoder_1_out12,
       decoder_1_out13, decoder_1_out14, decoder_1_out15, decoder_1_out16, decoder_1_out17, decoder_1_out18,
       decoder_1_out19, decoder_1_out20, decoder_1_out21, decoder_1_out22, decoder_1_out23, decoder_1_out24,
       decoder_1_out25, decoder_1_out26, EXECUTE, EXECUTE_FALLING, FETCH, I_type, IMM_11111, JAL, JALR,
       LOAD_OUT, LOADx, LUI, not_1_out, not_2_out, not_3_out, not_4_out, not_5_out, not_7_out, not_8_out,
       not_9_out, not_10_out, not_11_out, not_12_out, not_13_out, or_1_out, R_type, REGW, SFI, STORE_OUT,
       SUB_CARRY, SW, W_also_enable;
  wire [1:0] ASEL, B_INPUT, BSEL;
  wire [2:0] ALU_OP, ALUOP, multiplexer_4_out, REGDATASRC_OUT;
  wire [7:4] FLAG;
  wire [9:0] IMM9;
  wire [14:0] A_INPUT, ALU_OUT, IMM_9, multiplexer_1_out, multiplexer_2_out, multiplexer_3_out, REG_A_OUT,
       REG_B_OUT;
  wire [14:10] IMM_OUT;

  Multiplexer #(.select(2), .width(15)) multiplexer_1 (
    .in0(A_INPUT), .out(multiplexer_1_out), .sel(ASEL));  // open: in1, in2, in3
  ALU15 alu15_1 (
    .A(multiplexer_1_out), .B(multiplexer_2_out), .OP(multiplexer_4_out), .CIN(SUB_CARRY), .R(ALU_OUT));  // open: OIN, C, O, N, Z
  Multiplexer #(.select(2), .width(15)) multiplexer_2 (
    .in0(REG_B_OUT), .in1({IMM_OUT, IMM9}), .in3(IMM_9), .out(multiplexer_2_out), .sel(B_INPUT));  // open: in2
  and and_1 (and_1_out, REGW, EXECUTE);
  FLAGS8 flags8_1 (
    .NF(IB[7:0]), .WM({8{1'b1}}), .CLK(not_1_out), .F({FLAG[7], I, E, FLAG[4], O, C, N, Z}));  // open: IRQ
  not not_1 (not_1_out, CLK);
  Multiplexer #(.select(2), .width(15)) multiplexer_3 (
    .in0(ALU_OUT), .in1(DATAIN), .in2({IMM_OUT, IMM9}), .out(multiplexer_3_out),
    .sel({IMM_11111, DATA_SELECT}));  // open: in3
  Multiplexer #(.width(3)) multiplexer_4 (.in0(ALU_OP), .in1(3'b000), .out(multiplexer_4_out), .sel(or_1_out));
  or or_1 (or_1_out, DATA_SELECT, WE);
  not not_2 (not_2_out, IB[1]);
  not not_3 (not_3_out, IB[2]);
  not not_4 (not_4_out, IB[3]);
  not not_5 (not_5_out, IB[4]);
  REGS15 regs15_1 (
    .D(multiplexer_3_out), .W(and_1_out), .SelD(IB[7:5]), .CLK(CLK), .SelA(IB[10:8]), .SelB(IB[13:11]),
    .R0(R0), .R1(R1), .R2(R2), .R3(R3), .R4(R4), .R5(R5), .R6(R6), .R7(R7), .A(REG_A_OUT), .B(REG_B_OUT));
  or or_2 (BJumpEN, BZF, BNZF, BNF, BNNF, BCF, BNCF);
  and and_2 (SUB_CARRY, IB[0], not_2_out, not_3_out, not_4_out, not_5_out);
  Register #(.width(15)) INSTRUCTION_BUFFER (.D(DATAIN), .en(FETCH), .clk(CLK), .Q(IB));  // open: clr
  LED FETCH_DECODE (.in(FETCH));
  LED EXECUTE_WRITE (.in(EXECUTE));
  not not_6 (FETCH, EXECUTE);
  T_Flip_Flop t_ff_1 (.T(CLK), .clk(CLK), .Q(EXECUTE));  // open: Qn, reset, preset
  Multiplexer #(.width(3)) multiplexer_5 (.in0(ALUOP), .in1(3'b000), .out(ALU_OP), .sel(BJumpEN));
  D_Flip_Flop #(.trigger("falling")) d_ff_1 (.D(EXECUTE), .clk(CLK), .Q(EXECUTE_FALLING));  // open: Qn, preset, reset
  IMM15 imm15_1 (.INST(IB), .SEXT({IMM_OUT, IMM9}));
  and and_3 (BJumpPC_UPDATE, EXECUTE_FALLING, BJump);
  DECODE15 decode15_1 (
    .OPCODE(IB[4:0]), .STORE(STORE_OUT), .LOAD(LOAD_OUT), .ASEL(ASEL), .BSEL(BSEL), .ALUOP(ALUOP),
    .REGDATASRC(REGDATASRC_OUT), .REGW(REGW));  // open: in_2, in_3, in_5, in_4, SWI, FLAGSRC, FLAGWM, SRPW, SRFW
  not not_7 (not_7_out, Z);
  Multiplexer #(.width(2)) multiplexer_6 (.in0(BSEL), .in1(2'b11), .out(B_INPUT), .sel(BJumpEN));
  and and_4 (BZF, BJumpPC_UPDATE, Z);
  and and_5 (BNZF, BJumpPC_UPDATE, not_7_out);
  and and_6 (BNF, BJumpPC_UPDATE, N);
  and and_7 (BNNF, BJumpPC_UPDATE, not_8_out);
  not not_8 (not_8_out, N);
  and and_8 (BCF, BJumpPC_UPDATE, C);
  and and_9 (BNCF, BJumpPC_UPDATE, not_9_out);
  not not_9 (not_9_out, C);
  not not_10 (not_10_out, BJumpEN);
  Multiplexer #(.width(15)) multiplexer_7 (.in0(REG_A_OUT), .in1(PC), .out(A_INPUT), .sel(BJumpEN));
  Counter #(.max('h7fff), .trigger("falling"), .width(15)) Prgrm_Cntr (
    .load(BJumpPC_UPDATE), .D(ALU_OUT), .count(not_10_out), .Q(PC), .clk(EXECUTE), .clr(in_2));  // open: carry, up
  Decoder #(.select(5)) decoder_1 (
    .out0(decoder_1_out0), .out1(decoder_1_out1), .out2(decoder_1_out2), .out3(decoder_1_out3),
    .out4(decoder_1_out4), .out5(decoder_1_out5), .out6(decoder_1_out6), .out7(decoder_1_out7),
    .out8(decoder_1_out8), .out9(LOADx), .out10(decoder_1_out10), .out11(decoder_1_out11),
    .out12(decoder_1_out12), .out13(decoder_1_out13), .out14(decoder_1_out14), .out15(decoder_1_out15),
    .out16(decoder_1_out16), .out17(decoder_1_out17), .out18(decoder_1_out18), .out19(decoder_1_out19),
    .out20(decoder_1_out20), .out21(decoder_1_out21), .out22(decoder_1_out22), .out23(decoder_1_out23),
    .out24(decoder_1_out24), .out25(decoder_1_out25), .out26(decoder_1_out26), .out27(JALR), .out28(JAL),
    .out29(SFI), .out30(SW), .out31(LUI), .sel(IB[4:0]));  // open: en
  not not_11 (not_11_out, IB[1]);
  not not_12 (not_12_out, IB[2]);
  not not_13 (not_13_out, IB[4]);
  Multiplexer #(.width(15)) multiplexer_8 (.in0(ALU_OUT), .in1(PC), .out(ADDR), .sel(FETCH));
  assign DATAOUT = and_10_out ? REG_B_OUT : 15'bz;  // Controlled_Buffer controlled_buffer_1
  and and_10 (and_10_out, EXECUTE, WE);
  or or_3 (R_type, decoder_1_out0, decoder_1_out1, decoder_1_out2, decoder_1_out3, decoder_1_out4, decoder_1_out5, decoder_1_out6, decoder_1_out7);
  or or_4 (W_also_enable, decoder_1_out24, decoder_1_out25, decoder_1_out26, JALR, JAL, SFI, LUI);
  and and_11 (DATA_SELECT, IB[0], not_11_out, not_12_out, IB[3], not_13_out);
  and and_12 (IMM_11111, IB[0], IB[1], IB[2], IB[3], IB[4]);
  or or_5 (RE, FETCH, LOAD_OUT);
  and and_13 (WE, STORE_OUT, EXECUTE);
  or or_6 (I_type, decoder_1_out8, LOADx, decoder_1_out10, decoder_1_out11, decoder_1_out12, decoder_1_out13, decoder_1_out14, decoder_1_out15);
  or or_7 (BJump, decoder_1_out16, decoder_1_out17, decoder_1_out18, decoder_1_out19, decoder_1_out20, decoder_1_out21);

  // Other names for the same wires on the sheet: MUX_ADD_OR = DATA_SELECT; DATA[14:0] = DATAIN;
  //   FLAG (some bits) = {I, E, O, C, N, Z}; FLAGX[7:0] = IB[7:0]; RD_SEL[2:0] = IB[7:5]; FULL_OPCODE[4:0] = IB[4:0];
  //   IMM_OUT[9:0] = IMM9; MUX_ADD_OR_2 = WE; RE_a = FETCH; RS1_SEL[2:0] = IB[10:8]; RS2_SEL[2:0] = IB[13:11]

  // Notes on the sheet:
  //   B_TYPE
endmodule

module CHIPSET (
  input  RE,
  input  WE,
  input  [14:0] ADDR,
  input  [14:0] CPUDATAIN,
  input  KBIRQ,
  input  [6:0] KBDATA,
  input  CLK,
  output MEMCS,
  output TTYWR,
  output [14:0] IVECT,
  output TTYCLR,
  output [6:0] TTYDATA,
  output KBRD,
  output KBCLR,
  output [14:0] CPUDATAOUT,
  output IRQ,
  output [14:0] LED0,
  output [14:0] LED1,
  output [14:0] LED2,
  output [14:0] LED3,
  output [14:0] LED4,
  output [14:0] LED5,
  output [14:0] LED6,
  output [14:0] LED7,
  output [14:0] LED8,
  output [14:0] LED9,
  output [14:0] LEDA,
  output [14:0] LEDB,
  output [14:0] LEDC,
  output [14:0] LEDD,
  output [14:0] LEDE
);

  wire and_1_out, and_8_out, and_10_out, DATA7, IOCS, IVECTADDR, IVECTEN, IVECTRE, KBCS, LED0EN, LED0END,
       LED1EN, LED1END, LED2EN, LED2END, LED3EN, LED3END, LED4EN, LED4END, LED5EN, LED5END, LED6EN, LED6END,
       LED7EN, LED7END, LED8EN, LED8END, LED9EN, LED9END, LEDAEN, LEDAEND, LEDBEN, LEDBEND, LEDCEN, LEDCEND,
       LEDCS, LEDDEN, LEDDEND, LEDEEN, LEDEEND, LEDFEND, LEDRE, multiplexer_17_out, multiplexer_18_out, RWE,
       TTYCS;
  wire [14:0] DATAL0, DATAL1, DATAL2, DATAL3, DATAL4, DATAL5, DATAL6, DATAL7, DATAL8, DATAL9, DATALA, DATALB,
       DATALC, DATALD, DATALE, LEDDATA;
  wire [14:8] KBDATA15;

  assign CPUDATAOUT = KBRD ? {KBDATA15, DATA7, KBDATA} : 15'bz;  // Controlled_Buffer controlled_buffer_1
  assign CPUDATAOUT = LEDRE ? LEDDATA : 15'bz;  // Controlled_Buffer controlled_buffer_2
  assign CPUDATAOUT = IVECTRE ? IVECT : 15'bz;  // Controlled_Buffer controlled_buffer_3
  Register #(.width(15)) register_1 (.D(DATAL0), .en(LED0EN), .Q(LED0), .clk(CLK));  // open: clr
  Register #(.width(15)) register_2 (.D(DATAL1), .en(LED1EN), .Q(LED1), .clk(CLK));  // open: clr
  Register #(.width(15)) register_3 (.D(DATAL2), .en(LED2EN), .Q(LED2), .clk(CLK));  // open: clr
  Register #(.width(15)) register_4 (.D(DATAL3), .en(LED3EN), .Q(LED3), .clk(CLK));  // open: clr
  Register #(.width(15)) register_5 (.D(DATAL4), .en(LED4EN), .Q(LED4), .clk(CLK));  // open: clr
  and and_1 (and_1_out, WE, LEDCS);
  Decoder #(.select(4)) decoder_1 (
    .out0(LED0END), .out1(LED1END), .out2(LED2END), .out3(LED3END), .out4(LED4END), .out5(LED5END),
    .out6(LED6END), .out7(LED7END), .out8(LED8END), .out9(LED9END), .out10(LEDAEND), .out11(LEDBEND),
    .out12(LEDCEND), .out13(LEDDEND), .out14(LEDEEND), .out15(LEDFEND), .sel(ADDR[3:0]), .en(and_1_out));
  Register #(.width(15)) register_6 (.D(DATAL5), .en(LED5EN), .Q(LED5), .clk(CLK));  // open: clr
  Register #(.width(15)) register_7 (.D(DATAL6), .en(LED6EN), .Q(LED6), .clk(CLK));  // open: clr
  Register #(.width(15)) register_8 (.D(DATAL7), .en(LED7EN), .Q(LED7), .clk(CLK));  // open: clr
  Register #(.width(15)) register_9 (.D(DATAL8), .en(LED8EN), .Q(LED8), .clk(CLK));  // open: clr
  Register #(.width(15)) register_10 (.D(DATAL9), .en(LED9EN), .Q(LED9), .clk(CLK));  // open: clr
  or or_1 (LED0EN, LED0END, LEDFEND);
  or or_2 (LED1EN, LED1END, LEDFEND);
  or or_3 (LED2EN, LED2END, LEDFEND);
  or or_4 (LED3EN, LED3END, LEDFEND);
  or or_5 (LED4EN, LED4END, LEDFEND);
  or or_6 (LED5EN, LED5END, LEDFEND);
  or or_7 (LED6EN, LED6END, LEDFEND);
  or or_8 (LED7EN, LED7END, LEDFEND);
  or or_9 (LED8EN, LED8END, LEDFEND);
  or or_10 (LED9EN, LED9END, LEDFEND);
  or or_11 (LEDAEN, LEDAEND, LEDFEND);
  or or_12 (LEDBEN, LEDBEND, LEDFEND);
  or or_13 (LEDCEN, LEDCEND, LEDFEND);
  or or_14 (LEDDEN, LEDDEND, LEDFEND);
  or or_15 (LEDEEN, LEDEEND, LEDFEND);
  Pull_Resistor pull_resistor_1 (.node(KBDATA15[14]));
  Pull_Resistor pull_resistor_2 (.node(KBDATA15[13]));
  Pull_Resistor pull_resistor_3 (.node(KBDATA15[12]));
  Pull_Resistor pull_resistor_4 (.node(KBDATA15[11]));
  Pull_Resistor pull_resistor_5 (.node(KBDATA15[10]));
  Pull_Resistor pull_resistor_6 (.node(KBDATA15[9]));
  Pull_Resistor pull_resistor_7 (.node(KBDATA15[8]));
  Pull_Resistor pull_resistor_8 (.node(DATA7));
  Register #(.width(15)) register_11 (.D(DATALA), .en(LEDAEN), .Q(LEDA), .clk(CLK));  // open: clr
  Register #(.width(15)) register_12 (.D(DATALB), .en(LEDBEN), .Q(LEDB), .clk(CLK));  // open: clr
  Register #(.width(15)) register_13 (.D(DATALC), .en(LEDCEN), .Q(LEDC), .clk(CLK));  // open: clr
  Register #(.width(15)) register_14 (.D(DATALD), .en(LEDDEN), .Q(LEDD), .clk(CLK));  // open: clr
  Register #(.width(15)) register_15 (.D(DATALE), .en(LEDEEN), .Q(LEDE), .clk(CLK));  // open: clr
  Multiplexer #(.width(15)) multiplexer_1 (.in0(CPUDATAIN), .in1(LED1), .out(DATAL0), .sel(LEDFEND));
  Multiplexer #(.width(15)) multiplexer_2 (.in0(CPUDATAIN), .in1(LED2), .out(DATAL1), .sel(LEDFEND));
  Multiplexer #(.width(15)) multiplexer_3 (.in0(CPUDATAIN), .in1(LED3), .out(DATAL2), .sel(LEDFEND));
  Multiplexer #(.width(15)) multiplexer_4 (.in0(CPUDATAIN), .in1(LED4), .out(DATAL3), .sel(LEDFEND));
  Multiplexer #(.width(15)) multiplexer_5 (.in0(CPUDATAIN), .in1(LED5), .out(DATAL4), .sel(LEDFEND));
  Multiplexer #(.select(4), .width(15)) multiplexer_6 (
    .in0(LED0), .in1(LED1), .in2(LED2), .in3(LED3), .in4(LED4), .in5(LED5), .in6(LED6), .in7(LED7),
    .in8(LED8), .in9(LED9), .in10(LEDA), .in11(LEDB), .in12(LEDC), .in13(LEDD), .in14(LEDE),
    .in15({15{1'b0}}), .out(LEDDATA), .sel(ADDR[3:0]));
  Multiplexer #(.width(15)) multiplexer_7 (.in0(CPUDATAIN), .in1(LED6), .out(DATAL5), .sel(LEDFEND));
  Multiplexer #(.width(15)) multiplexer_8 (.in0(CPUDATAIN), .in1(LED7), .out(DATAL6), .sel(LEDFEND));
  Multiplexer #(.width(15)) multiplexer_9 (.in0(CPUDATAIN), .in1(LED8), .out(DATAL7), .sel(LEDFEND));
  Multiplexer #(.width(15)) multiplexer_10 (.in0(CPUDATAIN), .in1(LED9), .out(DATAL8), .sel(LEDFEND));
  Multiplexer #(.width(15)) multiplexer_11 (.in0(CPUDATAIN), .in1(LEDA), .out(DATAL9), .sel(LEDFEND));
  and and_2 (LEDRE, RE, LEDCS);
  Multiplexer #(.width(15)) multiplexer_12 (.in0(CPUDATAIN), .in1(LEDB), .out(DATALA), .sel(LEDFEND));
  Multiplexer #(.width(15)) multiplexer_13 (.in0(CPUDATAIN), .in1(LEDC), .out(DATALB), .sel(LEDFEND));
  Multiplexer #(.width(15)) multiplexer_14 (.in0(CPUDATAIN), .in1(LEDD), .out(DATALC), .sel(LEDFEND));
  Multiplexer #(.width(15)) multiplexer_15 (.in0(CPUDATAIN), .in1(LEDE), .out(DATALD), .sel(LEDFEND));
  Multiplexer #(.width(15)) multiplexer_16 (.in0(CPUDATAIN), .in1(CPUDATAIN), .out(DATALE), .sel(LEDFEND));
  and and_3 (IOCS, ADDR[5], ADDR[6], ADDR[7], ADDR[8], ADDR[9], ADDR[10], ADDR[11], ADDR[12], ADDR[13], ADDR[14], 1'b1);
  and and_4 (TTYCS, IOCS, ADDR[0], ~ADDR[1], ~ADDR[2], ~ADDR[3], ADDR[4]);  // AND_Gate
  and and_5 (KBCS, IOCS, ~ADDR[0], ~ADDR[1], ~ADDR[2], ~ADDR[3], ADDR[4]);  // AND_Gate
  and and_6 (IVECTADDR, ADDR[0], ADDR[1], ADDR[2], ADDR[3], ADDR[4], ADDR[5], ADDR[6], ADDR[7], ADDR[8], ADDR[9], ADDR[10], ADDR[11], ADDR[12], ADDR[13], ADDR[14]);
  and and_7 (TTYWR, TTYCS, WE);
  and and_8 (and_8_out, TTYWR, DATA7);
  and and_9 (KBRD, KBCS, RE);
  and and_10 (and_10_out, KBCS, WE);
  Multiplexer multiplexer_17 (.in0(and_10_out), .in1(1'b0), .out(multiplexer_17_out), .sel(KBCLR));
  and and_11 (LEDCS, IOCS, ~ADDR[4], RWE);  // AND_Gate
  and and_12 (IVECTEN, IVECTADDR, WE);
  and and_13 (IVECTRE, IVECTADDR, RE);
  or or_16 (RWE, RE, WE);
  and and_14 (MEMCS, ~IOCS, RWE);  // AND_Gate
  Multiplexer multiplexer_18 (.in0(and_8_out), .in1(1'b0), .out(multiplexer_18_out), .sel(TTYCLR));
  D_Flip_Flop d_ff_1 (.clk(CLK), .D(multiplexer_17_out), .Q(KBCLR));  // open: Qn, preset, reset
  Register #(.width(15)) register_16 (.D(CPUDATAIN), .en(IVECTEN), .Q(IVECT), .clk(CLK));  // open: clr
  D_Flip_Flop d_ff_2 (.clk(CLK), .D(multiplexer_18_out), .Q(TTYCLR));  // open: Qn, preset, reset

  assign IRQ = KBIRQ;
  assign TTYDATA = CPUDATAIN[6:0];

  // Other names for the same wires on the sheet: DATA[14:0] = CPUDATAIN; KBDATA15[7:0] = {DATA7, KBDATA}
endmodule

module ADDER15 (
  input  [14:0] A,
  input  [14:0] B,
  input  CIN,
  output COUT,
  output [14:0] S
);

  wire adder5_1_c_out, adder5_2_c_out;

  adder5 adder5_1 (.CARRY_IN(CIN), .B(B[4:0]), .A(A[4:0]), .RSULT(S[4:0]), .C_out(adder5_1_c_out));  // open: OVERFLOW
  adder5 adder5_2 (
    .CARRY_IN(adder5_1_c_out), .B(B[9:5]), .A(A[9:5]), .RSULT(S[9:5]), .C_out(adder5_2_c_out));  // open: OVERFLOW
  adder5 adder5_3 (
    .CARRY_IN(adder5_2_c_out), .B(B[14:10]), .A(A[14:10]), .RSULT(S[14:10]), .C_out(COUT));  // open: OVERFLOW

  // Other names for the same wires on the sheet: A1[4:0] = A[4:0]; A2[4:0] = A[9:5]; A3[4:0] = A[14:10];
  //   B1[4:0] = B[4:0]; B2[4:0] = B[9:5]; B3[4:0] = B[14:10]; S1[4:0] = S[4:0]; S2[4:0] = S[9:5]; S3[4:0] = S[14:10]
endmodule

module REGS15 (
  input  [14:0] D,
  input  W,
  input  [2:0] SelD,
  input  CLK,
  input  [2:0] SelA,
  input  [2:0] SelB,
  output [14:0] R0,
  output [14:0] R1,
  output [14:0] R2,
  output [14:0] R3,
  output [14:0] R4,
  output [14:0] R5,
  output [14:0] R6,
  output [14:0] R7,
  output [14:0] A,
  output [14:0] B
);

  wire W_1, W_2, W_3, W_4, W_5, W_6, W_7;

  Register #(.trigger("falling"), .width(15)) register_1 (.D({15{1'b0}}), .clk(CLK), .Q(R0));  // open: en, clr
  Decoder #(.select(3)) decoder_1 (
    .out1(W_1), .out2(W_2), .out3(W_3), .out4(W_4), .out5(W_5), .out6(W_6), .out7(W_7), .sel(SelD), .en(W));  // open: out0
  Multiplexer #(.select(3), .width(15)) multiplexer_1 (
    .in0(R0), .in1(R1), .in2(R2), .in3(R3), .in4(R4), .in5(R5), .in6(R6), .in7(R7), .out(A), .sel(SelA));
  Register #(.trigger("falling"), .width(15)) register_2 (.D(D), .en(W_1), .clk(CLK), .Q(R1));  // open: clr
  Register #(.trigger("falling"), .width(15)) register_3 (.D(D), .en(W_2), .clk(CLK), .Q(R2));  // open: clr
  Register #(.trigger("falling"), .width(15)) register_4 (.D(D), .en(W_3), .clk(CLK), .Q(R3));  // open: clr
  Multiplexer #(.select(3), .width(15)) multiplexer_2 (
    .in0(R0), .in1(R1), .in2(R2), .in3(R3), .in4(R4), .in5(R5), .in6(R6), .in7(R7), .out(B), .sel(SelB));
  Register #(.trigger("falling"), .width(15)) register_5 (.D(D), .en(W_4), .clk(CLK), .Q(R4));  // open: clr
  Register #(.trigger("falling"), .width(15)) register_6 (.D(D), .en(W_5), .clk(CLK), .Q(R5));  // open: clr
  Register #(.trigger("falling"), .width(15)) register_7 (.D(D), .en(W_6), .clk(CLK), .Q(R6));  // open: clr
  Register #(.trigger("falling"), .width(15)) register_8 (.D(D), .en(W_7), .clk(CLK), .Q(R7));  // open: clr
endmodule

module ALU15 (
  input  [14:0] A,
  input  [14:0] B,
  input  [2:0] OP,
  input  CIN,
  input  OIN,
  output C,
  output O,
  output N,
  output Z,
  output [14:0] R
);

  wire ADD_C, ADD_OVERFLOW, adder5_1_c_out, adder5_2_c_out, adder5_3_c_out, adder5_4_c_out, CHECK_ZERO,
       NEGATIVE, SUB_C, SUB_OVERFLOW;
  wire [4:0] not_1_out, not_2_out, not_4_out;
  wire [14:0] ADD_R, AND_R, not_3_out, OR_R, SLL_R, SRA_R, SRL_R, SUB_R, XOR_R;

  assign not_1_out = ~B[4:0];  // NOT_Gate not_1, 5 bits wide
  assign AND_R = A & B;  // AND_Gate and_1, 15 bits wide
  assign OR_R = A | B;  // OR_Gate or_1, 15 bits wide
  assign XOR_R = A ^ B;  // XOR_Gate xor_1, 15 bits wide
  nor nor_1 (CHECK_ZERO, R[0], R[1], R[2], R[3], R[4], R[5], R[6], R[7], R[8], R[9], R[10], R[11], R[12], R[13], R[14]);
  adder5 adder5_1 (.CARRY_IN(CIN), .B(B[4:0]), .A(A[4:0]), .C_out(adder5_1_c_out));  // open: RSULT, OVERFLOW
  adder5 adder5_2 (.CARRY_IN(CIN), .B(not_1_out), .A(A[4:0]), .C_out(adder5_2_c_out));  // open: RSULT, OVERFLOW
  and and_2 (NEGATIVE, 1'b1, R[14]);
  logicalshifter15 logicalshifter15_1 (.S(B[3:0]), .left(A), .right(A), .result(SLL_R), .result2(SRL_R));
  ArShiftRight arshiftright_1 (.Selection(B[3:0]), .inputz(A), .ResultAS(SRA_R));
  assign not_2_out = ~B[9:5];  // NOT_Gate not_2, 5 bits wide
  adder5 adder5_3 (.CARRY_IN(adder5_1_c_out), .B(B[9:5]), .A(A[9:5]), .C_out(adder5_3_c_out));  // open: RSULT, OVERFLOW
  adder5 adder5_4 (
    .CARRY_IN(adder5_2_c_out), .B(not_2_out), .A(A[9:5]), .C_out(adder5_4_c_out));  // open: RSULT, OVERFLOW
  Multiplexer #(.select(3), .width(15)) multiplexer_1 (
    .in0(ADD_R), .in1(SUB_R), .in2(AND_R), .in3(OR_R), .in4(XOR_R), .in5(SLL_R), .in6(SRL_R), .in7(SRA_R),
    .out(R), .sel(OP));
  assign not_3_out = ~B;  // NOT_Gate not_3, 15 bits wide
  ADDER15 adder15_1 (.A(A), .B(not_3_out), .CIN(CIN), .COUT(SUB_C), .S(SUB_R));
  assign not_4_out = ~B[14:10];  // NOT_Gate not_4, 5 bits wide
  Multiplexer #(.select(3)) multiplexer_2 (
    .in0(NEGATIVE), .in1(NEGATIVE), .in2(NEGATIVE), .in3(NEGATIVE), .in4(NEGATIVE), .in5(NEGATIVE),
    .in6(NEGATIVE), .in7(NEGATIVE), .out(N), .sel(OP));
  adder5 adder5_5 (
    .CARRY_IN(adder5_3_c_out), .B(B[14:10]), .A(A[14:10]), .OVERFLOW(ADD_OVERFLOW));  // open: RSULT, C_out
  Multiplexer #(.select(3)) multiplexer_3 (
    .in0(CHECK_ZERO), .in1(CHECK_ZERO), .in2(CHECK_ZERO), .in3(CHECK_ZERO), .in4(CHECK_ZERO),
    .in5(CHECK_ZERO), .in6(CHECK_ZERO), .in7(CHECK_ZERO), .out(Z), .sel(OP));
  adder5 adder5_6 (
    .CARRY_IN(adder5_4_c_out), .B(not_4_out), .A(A[14:10]), .OVERFLOW(SUB_OVERFLOW));  // open: RSULT, C_out
  ADDER15 adder15_2 (.A(A), .B(B), .CIN(CIN), .COUT(ADD_C), .S(ADD_R));
  Multiplexer #(.select(2)) multiplexer_4 (.in0(ADD_C), .in1(SUB_C), .out(C), .sel(OP[1:0]));  // open: in2, in3
  Multiplexer #(.select(2)) multiplexer_5 (
    .in0(ADD_OVERFLOW), .in1(SUB_OVERFLOW), .out(O), .sel(OP[1:0]));  // open: in2, in3

  // Other names for the same wires on the sheet: A1[4:0] = A[4:0]; A2[4:0] = A[9:5]; A3[4:0] = A[14:10];
  //   B1[4:0] = B[4:0]; B2[4:0] = B[9:5]; B3[4:0] = B[14:10]; Bs[3:0] = B[3:0]; OP_C[1:0] = OP[1:0]; R1[4:0] = R[4:0];
  //   R2[4:0] = R[9:5]; R3[4:0] = R[14:10]

  // Notes on the sheet:
  //   0001 = 1 shift. 1101 = 13 shift, 1110 = 14 shift(all zero)
  //   OVERFLOW ADD
  //   OVERFLOW SUB
endmodule

module FLAGS8 (
  input  IRQ,
  input  [7:0] NF,
  input  [7:0] WM,
  input  CLK,
  output [7:0] F
);

  Register #(.width(1)) register_1 (.D(1'b0), .en(1'b0), .clk(CLK), .Q(F[7]));  // open: clr
  Register #(.width(1)) register_2 (.D(NF[6]), .en(WM[6]), .clk(CLK), .Q(F[6]));  // open: clr
  Register #(.width(1)) register_3 (.D(NF[5]), .en(WM[5]), .clk(CLK), .Q(F[5]));  // open: clr
  Register #(.width(1)) register_4 (.D(1'b0), .en(1'b0), .clk(CLK), .Q(F[4]));  // open: clr
  Register #(.width(1)) register_5 (.D(NF[3]), .en(WM[3]), .clk(CLK), .Q(F[3]));  // open: clr
  Register #(.width(1)) register_6 (.D(NF[2]), .en(WM[2]), .clk(CLK), .Q(F[2]));  // open: clr
  Register #(.width(1)) register_7 (.D(NF[1]), .en(WM[1]), .clk(CLK), .Q(F[1]));  // open: clr
  Register #(.width(1)) register_8 (.D(NF[0]), .en(WM[0]), .clk(CLK), .Q(F[0]));  // open: clr

  // Other names for the same wires on the sheet: Z_FLAG_OUT = F[0]; N_FLAG_OUT = F[1]; C_FLAG_OUT = F[2];
  //   O_FLAG_OUT = F[3]; FLAG_4_OUT = F[4]; E_FLAG_OUT = F[5]; I_FLAG_OUT = F[6]; FLAG_7_OUT = F[7];
  //   Z_FLAG_IN = NF[0]; N_FLAG_IN = NF[1]; C_FLAG_IN = NF[2]; O_FLAG_IN = NF[3]; E_FLAG_IN = NF[5];
  //   I_FLAG_IN = NF[6]; Z_FLAG_ENABLE = WM[0]; N_FLAG_ENABLE = WM[1]; C_FLAG_ENABLE = WM[2]; O_FLAG_ENABLE = WM[3];
  //   E_FLAG_ENABLE = WM[5]; I_FLAG_ENABLE = WM[6]
endmodule

module IMM15 (
  input  [14:0] INST,
  output [14:0] SEXT
);

  wire and_1_out, and_2_out, and_3_out, and_4_out, and_6_out, and_7_out, Encode_0_a, Encode_0_b, Encode_0_c,
       Encode_1_a, Encode_2_a, not_6_out, not_7_out, NOT_OP_0, NOT_OP_1, NOT_OP_2, NOT_OP_3, NOT_OP_4;
  wire [2:0] or_5_out;

  and and_1 (and_1_out, INST[3], NOT_OP_4);
  and and_2 (and_2_out, INST[0], INST[1], NOT_OP_2, INST[3], INST[4]);
  and and_3 (and_3_out, INST[4], INST[3], INST[2], NOT_OP_1, NOT_OP_0);
  and and_4 (and_4_out, INST[4], INST[3], INST[2], NOT_OP_1, INST[0]);
  and and_5 (Encode_0_c, INST[4], INST[3], INST[2], INST[1], INST[0]);
  or or_1 (Encode_0_b, and_3_out, and_4_out);
  LED Bits_11 (.in(Encode_0_c));
  not not_1 (NOT_OP_0, INST[0]);
  not not_2 (NOT_OP_1, INST[1]);
  not not_3 (NOT_OP_2, INST[2]);
  not not_4 (NOT_OP_3, INST[3]);
  not not_5 (NOT_OP_4, INST[4]);
  or or_2 (Encode_0_a, and_1_out, and_2_out);
  LED Bits_4 (.in(Encode_0_a));
  LED Bits_7 (.in(Encode_0_b));
  Register #(.trigger("high"), .width(15)) register_1 (.D(SEXT), .en(1'b1), .clk(1'b1));  // open: Q, clr
  and and_6 (and_6_out, INST[2], INST[1], NOT_OP_0);
  and and_7 (and_7_out, INST[2], INST[1], INST[0]);
  or or_3 (or_5_out[2], Encode_0_c, Encode_2_a);
  not not_6 (not_6_out, and_6_out);
  not not_7 (not_7_out, and_7_out);
  or or_4 (or_5_out[1], Encode_0_b, Encode_1_a);
  and and_8 (Encode_1_a, INST[4], NOT_OP_3, not_6_out, not_7_out);
  and and_9 (Encode_2_a, INST[4], INST[3], INST[2], INST[1], NOT_OP_0);
  Multiplexer #(.select(3), .width(15)) multiplexer_1 (
    .in0({15{1'b0}}), .in1({{12{INST[14]}}, INST[13:11]}), .in2({{6{INST[14]}}, INST[13:5]}),
    .in3({{9{INST[14]}}, INST[13:8]}), .in4({{12{INST[14]}}, INST[7:5]}),
    .in5({{5{INST[14]}}, INST[13:8], 4'b0000}), .in6({15{1'b0}}), .in7({15{1'b0}}), .out(SEXT), .sel(or_5_out));
  LED Bits_10 (.in(Encode_1_a));
  or or_5 (or_5_out[0], Encode_0_c, Encode_0_b, Encode_0_a);
  LED Bits_4_SW (.in(Encode_2_a));

  // Other names for the same wires on the sheet: Bits_4_SW[14:0] = {{12{INST[14]}}, INST[7:5]};
  //   Bits_10[14:0] = {{6{INST[14]}}, INST[13:5]}; Bits_4[14:0] = {{12{INST[14]}}, INST[13:11]};
  //   Bits_7[14:0] = {{9{INST[14]}}, INST[13:8]}; Bits_11[14:4] = {{5{INST[14]}}, INST[13:8]};
  //   Encode_1_b = Encode_0_b; Encode_2_b = Encode_0_c; OP_0 = INST[0]; OP_1 = INST[1]; OP_2 = INST[2];
  //   OP_3 = INST[3]; OP_4 = INST[4]
endmodule

module DECODE15 (
  input  [4:0] OPCODE,
  input  in_2,
  input  in_3,
  input  in_4,
  input  in_5,
  output SWI,
  output STORE,
  output LOAD,
  output [1:0] ASEL,
  output [1:0] BSEL,
  output [2:0] ALUOP,
  output [2:0] REGDATASRC,
  output REGW,
  output [1:0] FLAGSRC,
  output [7:0] FLAGWM,
  output SRPW,
  output SRFW
);

  wire and_3_out, and_4_out, and_5_out, and_6_out, and_7_out, and_8_out, BSEL_0_SET_a, BSEL_0_SET_b,
       not_1_out, NOT_DC_OP_0, NOT_DC_OP_1, NOT_DC_OP_3, NOT_DC_OP_4;

  and and_1 (BSEL_0_SET_b, OPCODE[4], OPCODE[3], OPCODE[2], OPCODE[1], NOT_DC_OP_0);
  and and_2 (BSEL_0_SET_a, NOT_DC_OP_4, OPCODE[3]);
  and and_3 (and_3_out, NOT_DC_OP_4, NOT_DC_OP_3);
  and and_4 (and_4_out, NOT_DC_OP_4, OPCODE[3]);
  and and_5 (and_5_out, OPCODE[4], OPCODE[3]);
  and and_6 (and_6_out, OPCODE[4], OPCODE[3], OPCODE[2], OPCODE[1], NOT_DC_OP_0);
  and and_7 (and_7_out, and_5_out, not_1_out);
  not not_1 (not_1_out, and_6_out);
  not not_2 (NOT_DC_OP_0, OPCODE[0]);
  not not_3 (NOT_DC_OP_1, OPCODE[1]);
  not not_4 (NOT_DC_OP_1, OPCODE[2]);
  not not_5 (NOT_DC_OP_3, OPCODE[3]);
  not not_6 (NOT_DC_OP_4, OPCODE[4]);
  and and_8 (and_8_out, NOT_DC_OP_4, OPCODE[3], NOT_DC_OP_1, NOT_DC_OP_1);
  buf or_1 (ASEL[0], in_2);  // OR_Gate
  buf or_2 (ASEL[1], in_3);  // OR_Gate
  and and_9 (STORE, OPCODE[4], OPCODE[3], OPCODE[2], OPCODE[1], NOT_DC_OP_0);
  and and_10 (LOAD, NOT_DC_OP_4, OPCODE[3], NOT_DC_OP_1, NOT_DC_OP_1, OPCODE[0]);
  or or_3 (BSEL[0], BSEL_0_SET_a, BSEL_0_SET_b);
  buf or_4 (BSEL[1], in_4);  // OR_Gate
  buf or_5 (REGDATASRC[0], in_5);  // OR_Gate
  buf or_6 (REGDATASRC[1], in_5);  // OR_Gate
  buf or_7 (REGDATASRC[2], in_5);  // OR_Gate
  or or_8 (REGW, and_3_out, and_4_out, and_7_out);
  and and_11 (SWI, OPCODE[4], NOT_DC_OP_3, OPCODE[2], OPCODE[1], OPCODE[0]);

  assign ALUOP = OPCODE[2:0];

  // Other names for the same wires on the sheet: DC_OP_0 = OPCODE[0]; DC_OP_1 = OPCODE[1]; DC_OP_2 = OPCODE[2];
  //   NOT_DC_OP_2 = NOT_DC_OP_1; DC_OP_3 = OPCODE[3]; DC_OP_4 = OPCODE[4]
endmodule

module ArShiftRight (
  input  [3:0] Selection,
  input  [14:0] inputz,
  output [14:0] ResultAS
);

  Multiplexer #(.select(4)) multiplexer_1 (
    .in0(inputz[0]), .in1(inputz[1]), .in2(inputz[2]), .in3(inputz[3]), .in4(inputz[4]), .in5(inputz[5]),
    .in6(inputz[6]), .in7(inputz[7]), .in8(inputz[8]), .in9(inputz[9]), .in10(inputz[10]), .in11(inputz[11]),
    .in12(inputz[12]), .in13(inputz[13]), .in14(inputz[14]), .out(ResultAS[0]), .sel(Selection));  // open: in15
  Multiplexer #(.select(4)) multiplexer_2 (
    .in0(inputz[1]), .in1(inputz[2]), .in2(inputz[3]), .in3(inputz[4]), .in4(inputz[5]), .in5(inputz[6]),
    .in6(inputz[7]), .in7(inputz[8]), .in8(inputz[9]), .in9(inputz[10]), .in10(inputz[11]),
    .in11(inputz[12]), .in12(inputz[13]), .in13(inputz[14]), .in14(inputz[14]), .out(ResultAS[1]),
    .sel(Selection));  // open: in15
  Multiplexer #(.select(4)) multiplexer_3 (
    .in0(inputz[2]), .in1(inputz[3]), .in2(inputz[4]), .in3(inputz[5]), .in4(inputz[6]), .in5(inputz[7]),
    .in6(inputz[8]), .in7(inputz[9]), .in8(inputz[10]), .in9(inputz[11]), .in10(inputz[12]),
    .in11(inputz[13]), .in12(inputz[14]), .in13(inputz[14]), .in14(inputz[14]), .out(ResultAS[2]),
    .sel(Selection));  // open: in15
  Multiplexer #(.select(4)) multiplexer_4 (
    .in0(inputz[3]), .in1(inputz[4]), .in2(inputz[5]), .in3(inputz[6]), .in4(inputz[7]), .in5(inputz[8]),
    .in6(inputz[9]), .in7(inputz[10]), .in8(inputz[11]), .in9(inputz[12]), .in10(inputz[13]),
    .in11(inputz[14]), .in12(inputz[14]), .in13(inputz[14]), .in14(inputz[14]), .out(ResultAS[3]),
    .sel(Selection));  // open: in15
  Multiplexer #(.select(4)) multiplexer_5 (
    .in0(inputz[4]), .in1(inputz[5]), .in2(inputz[6]), .in3(inputz[7]), .in4(inputz[8]), .in5(inputz[9]),
    .in6(inputz[10]), .in7(inputz[11]), .in8(inputz[12]), .in9(inputz[13]), .in10(inputz[14]),
    .in11(inputz[14]), .in12(inputz[14]), .in13(inputz[14]), .in14(inputz[14]), .out(ResultAS[4]),
    .sel(Selection));  // open: in15
  Multiplexer #(.select(4)) multiplexer_6 (
    .in0(inputz[5]), .in1(inputz[6]), .in2(inputz[7]), .in3(inputz[8]), .in4(inputz[9]), .in5(inputz[10]),
    .in6(inputz[11]), .in7(inputz[12]), .in8(inputz[13]), .in9(inputz[14]), .in10(inputz[14]),
    .in11(inputz[14]), .in12(inputz[14]), .in13(inputz[14]), .in14(inputz[14]), .out(ResultAS[5]),
    .sel(Selection));  // open: in15
  Multiplexer #(.select(4)) multiplexer_7 (
    .in0(inputz[6]), .in1(inputz[7]), .in2(inputz[8]), .in3(inputz[9]), .in4(inputz[10]), .in5(inputz[11]),
    .in6(inputz[12]), .in7(inputz[13]), .in8(inputz[14]), .in9(inputz[14]), .in10(inputz[14]),
    .in11(inputz[14]), .in12(inputz[14]), .in13(inputz[14]), .in14(inputz[14]), .out(ResultAS[6]),
    .sel(Selection));  // open: in15
  Multiplexer #(.select(4)) multiplexer_8 (
    .in0(inputz[7]), .in1(inputz[8]), .in2(inputz[9]), .in3(inputz[10]), .in4(inputz[11]), .in5(inputz[12]),
    .in6(inputz[13]), .in7(inputz[14]), .in8(inputz[14]), .in9(inputz[14]), .in10(inputz[14]),
    .in11(inputz[14]), .in12(inputz[14]), .in13(inputz[14]), .in14(inputz[14]), .out(ResultAS[7]),
    .sel(Selection));  // open: in15
  Multiplexer #(.select(4)) multiplexer_9 (
    .in0(inputz[8]), .in1(inputz[9]), .in2(inputz[10]), .in3(inputz[11]), .in4(inputz[12]), .in5(inputz[13]),
    .in6(inputz[14]), .in7(inputz[14]), .in8(inputz[14]), .in9(inputz[14]), .in10(inputz[14]),
    .in11(inputz[14]), .in12(inputz[14]), .in13(inputz[14]), .in14(inputz[14]), .out(ResultAS[8]),
    .sel(Selection));  // open: in15
  Multiplexer #(.select(4)) multiplexer_10 (
    .in0(inputz[9]), .in1(inputz[10]), .in2(inputz[11]), .in3(inputz[12]), .in4(inputz[13]),
    .in5(inputz[14]), .in6(inputz[14]), .in7(inputz[14]), .in8(inputz[14]), .in9(inputz[14]),
    .in10(inputz[14]), .in11(inputz[14]), .in12(inputz[14]), .in13(inputz[14]), .in14(inputz[14]),
    .out(ResultAS[9]), .sel(Selection));  // open: in15
  Multiplexer #(.select(4)) multiplexer_11 (
    .in0(inputz[10]), .in1(inputz[11]), .in2(inputz[12]), .in3(inputz[13]), .in4(inputz[14]),
    .in5(inputz[14]), .in6(inputz[14]), .in7(inputz[14]), .in8(inputz[14]), .in9(inputz[14]),
    .in10(inputz[14]), .in11(inputz[14]), .in12(inputz[14]), .in13(inputz[14]), .in14(inputz[14]),
    .out(ResultAS[10]), .sel(Selection));  // open: in15
  Multiplexer #(.select(4)) multiplexer_12 (
    .in0(inputz[11]), .in1(inputz[12]), .in2(inputz[13]), .in3(inputz[14]), .in4(inputz[14]),
    .in5(inputz[14]), .in6(inputz[14]), .in7(inputz[14]), .in8(inputz[14]), .in9(inputz[14]),
    .in10(inputz[14]), .in11(inputz[14]), .in12(inputz[14]), .in13(inputz[14]), .in14(inputz[14]),
    .out(ResultAS[11]), .sel(Selection));  // open: in15
  Multiplexer #(.select(4)) multiplexer_13 (
    .in0(inputz[12]), .in1(inputz[13]), .in2(inputz[14]), .in3(inputz[14]), .in4(inputz[14]),
    .in5(inputz[14]), .in6(inputz[14]), .in7(inputz[14]), .in8(inputz[14]), .in9(inputz[14]),
    .in10(inputz[14]), .in11(inputz[14]), .in12(inputz[14]), .in13(inputz[14]), .in14(inputz[14]),
    .out(ResultAS[12]), .sel(Selection));  // open: in15
  Multiplexer #(.select(4)) multiplexer_14 (
    .in0(inputz[13]), .in1(inputz[14]), .in2(inputz[14]), .in3(inputz[14]), .in4(inputz[14]),
    .in5(inputz[14]), .in6(inputz[14]), .in7(inputz[14]), .in8(inputz[14]), .in9(inputz[14]),
    .in10(inputz[14]), .in11(inputz[14]), .in12(inputz[14]), .in13(inputz[14]), .in14(inputz[14]),
    .out(ResultAS[13]), .sel(Selection));  // open: in15
  Multiplexer #(.select(4)) multiplexer_15 (
    .in0(inputz[14]), .in1(inputz[14]), .in2(inputz[14]), .in3(inputz[14]), .in4(inputz[14]),
    .in5(inputz[14]), .in6(inputz[14]), .in7(inputz[14]), .in8(inputz[14]), .in9(inputz[14]),
    .in10(inputz[14]), .in11(inputz[14]), .in12(inputz[14]), .in13(inputz[14]), .in14(inputz[14]),
    .out(ResultAS[14]), .sel(Selection));  // open: in15

  // Other names for the same wires on the sheet: Z0 = ResultAS[0]; Z1 = ResultAS[1]; Z2 = ResultAS[2];
  //   Z3 = ResultAS[3]; Z4 = ResultAS[4]; Z5 = ResultAS[5]; Z6 = ResultAS[6]; Z7 = ResultAS[7]; Z8 = ResultAS[8];
  //   Z9 = ResultAS[9]; Z10 = ResultAS[10]; Z11 = ResultAS[11]; Z12 = ResultAS[12]; Z13 = ResultAS[13];
  //   Z14 = ResultAS[14]

  // Notes on the sheet:
  //   A14
  //   A13
  //   A12
  //   A11
  //   A10
  //   A9
  //   A8
  //   A7
  //   A6
  //   A4
  //   A5
  //   A3
  //   A1
  //   A2
  //   A0
endmodule

module logicalshifter15 (
  input  [3:0] S,
  input  [14:0] left,
  input  [14:0] right,
  output [14:0] result,
  output [14:0] result2
);

  Multiplexer #(.select(4)) multiplexer_1 (
    .in0(left[14]), .in1(left[13]), .in2(left[12]), .in3(left[11]), .in4(left[10]), .in5(left[9]),
    .in6(left[8]), .in7(left[7]), .in8(left[6]), .in9(left[5]), .in10(left[4]), .in11(left[3]),
    .in12(left[2]), .in13(left[1]), .in14(left[0]), .out(result[14]), .sel(S));  // open: in15
  Multiplexer #(.select(4)) multiplexer_2 (
    .in0(left[13]), .in1(left[12]), .in2(left[11]), .in3(left[10]), .in4(left[9]), .in5(left[8]),
    .in6(left[7]), .in7(left[6]), .in8(left[5]), .in9(left[4]), .in10(left[3]), .in11(left[2]),
    .in12(left[1]), .in13(left[0]), .in14(1'b0), .out(result[13]), .sel(S));  // open: in15
  Multiplexer #(.select(4)) multiplexer_3 (
    .in0(left[12]), .in1(left[11]), .in2(left[10]), .in3(left[9]), .in4(left[8]), .in5(left[7]),
    .in6(left[6]), .in7(left[5]), .in8(left[4]), .in9(left[3]), .in10(left[2]), .in11(left[1]),
    .in12(left[0]), .in13(1'b0), .in14(1'b0), .out(result[12]), .sel(S));  // open: in15
  Multiplexer #(.select(4)) multiplexer_4 (
    .in0(left[11]), .in1(left[10]), .in2(left[9]), .in3(left[8]), .in4(left[7]), .in5(left[6]),
    .in6(left[5]), .in7(left[4]), .in8(left[3]), .in9(left[2]), .in10(left[1]), .in11(left[0]), .in12(1'b0),
    .in13(1'b0), .in14(1'b0), .out(result[11]), .sel(S));  // open: in15
  Multiplexer #(.select(4)) multiplexer_5 (
    .in0(left[10]), .in1(left[9]), .in2(left[8]), .in3(left[7]), .in4(left[6]), .in5(left[5]), .in6(left[4]),
    .in7(left[3]), .in8(left[2]), .in9(left[1]), .in10(left[0]), .in11(1'b0), .in12(1'b0), .in13(1'b0),
    .in14(1'b0), .out(result[10]), .sel(S));  // open: in15
  Multiplexer #(.select(4)) multiplexer_6 (
    .in0(left[9]), .in1(left[8]), .in2(left[7]), .in3(left[6]), .in4(left[5]), .in5(left[4]), .in6(left[3]),
    .in7(left[2]), .in8(left[1]), .in9(left[0]), .in10(1'b0), .in11(1'b0), .in12(1'b0), .in13(1'b0),
    .in14(1'b0), .out(result[9]), .sel(S));  // open: in15
  Multiplexer #(.select(4)) multiplexer_7 (
    .in0(left[8]), .in1(left[7]), .in2(left[6]), .in3(left[5]), .in4(left[4]), .in5(left[3]), .in6(left[2]),
    .in7(left[1]), .in8(left[0]), .in9(1'b0), .in10(1'b0), .in11(1'b0), .in12(1'b0), .in13(1'b0),
    .in14(1'b0), .out(result[8]), .sel(S));  // open: in15
  Multiplexer #(.select(4)) multiplexer_8 (
    .in0(left[7]), .in1(left[6]), .in2(left[5]), .in3(left[4]), .in4(left[3]), .in5(left[2]), .in6(left[1]),
    .in7(left[0]), .in8(1'b0), .in9(1'b0), .in10(1'b0), .in11(1'b0), .in12(1'b0), .in13(1'b0), .in14(1'b0),
    .out(result[7]), .sel(S));  // open: in15
  Multiplexer #(.select(4)) multiplexer_9 (
    .in0(left[6]), .in1(left[5]), .in2(left[4]), .in3(left[3]), .in4(left[2]), .in5(left[1]), .in6(left[0]),
    .in7(1'b0), .in8(1'b0), .in9(1'b0), .in10(1'b0), .in11(1'b0), .in12(1'b0), .in13(1'b0), .in14(1'b0),
    .out(result[6]), .sel(S));  // open: in15
  Multiplexer #(.select(4)) multiplexer_10 (
    .in0(left[5]), .in1(left[4]), .in2(left[3]), .in3(left[2]), .in4(left[1]), .in5(left[0]), .in6(1'b0),
    .in7(1'b0), .in8(1'b0), .in9(1'b0), .in10(1'b0), .in11(1'b0), .in12(1'b0), .in13(1'b0), .in14(1'b0),
    .out(result[5]), .sel(S));  // open: in15
  Multiplexer #(.select(4)) multiplexer_11 (
    .in0(left[4]), .in1(left[3]), .in2(left[2]), .in3(left[1]), .in4(left[0]), .in5(1'b0), .in6(1'b0),
    .in7(1'b0), .in8(1'b0), .in9(1'b0), .in10(1'b0), .in11(1'b0), .in12(1'b0), .in13(1'b0), .in14(1'b0),
    .out(result[4]), .sel(S));  // open: in15
  Multiplexer #(.select(4)) multiplexer_12 (
    .in0(left[3]), .in1(left[2]), .in2(left[1]), .in3(left[0]), .in4(1'b0), .in5(1'b0), .in6(1'b0),
    .in7(1'b0), .in8(1'b0), .in9(1'b0), .in10(1'b0), .in11(1'b0), .in12(1'b0), .in13(1'b0), .in14(1'b0),
    .out(result[3]), .sel(S));  // open: in15
  Multiplexer #(.select(4)) multiplexer_13 (
    .in0(left[2]), .in1(left[1]), .in2(left[0]), .in3(1'b0), .in4(1'b0), .in5(1'b0), .in6(1'b0), .in7(1'b0),
    .in8(1'b0), .in9(1'b0), .in10(1'b0), .in11(1'b0), .in12(1'b0), .in13(1'b0), .in14(1'b0), .out(result[2]),
    .sel(S));  // open: in15
  Multiplexer #(.select(4)) multiplexer_14 (
    .in0(left[1]), .in1(left[0]), .in2(1'b0), .in3(1'b0), .in4(1'b0), .in5(1'b0), .in6(1'b0), .in7(1'b0),
    .in8(1'b0), .in9(1'b0), .in10(1'b0), .in11(1'b0), .in12(1'b0), .in13(1'b0), .in14(1'b0), .out(result[1]),
    .sel(S));  // open: in15
  Multiplexer #(.select(4)) multiplexer_15 (
    .in0(left[0]), .in1(1'b0), .in2(1'b0), .in3(1'b0), .in4(1'b0), .in5(1'b0), .in6(1'b0), .in7(1'b0),
    .in8(1'b0), .in9(1'b0), .in10(1'b0), .in11(1'b0), .in12(1'b0), .in13(1'b0), .in14(1'b0), .out(result[0]),
    .sel(S));  // open: in15
  Multiplexer #(.select(4)) multiplexer_16 (
    .in0(right[0]), .in1(right[1]), .in2(right[2]), .in3(right[3]), .in4(right[4]), .in5(right[5]),
    .in6(right[6]), .in7(right[7]), .in8(right[8]), .in9(right[9]), .in10(right[10]), .in11(right[11]),
    .in12(right[12]), .in13(right[13]), .in14(right[14]), .out(result2[0]), .sel(S));  // open: in15
  Multiplexer #(.select(4)) multiplexer_17 (
    .in0(right[1]), .in1(right[2]), .in2(right[3]), .in3(right[4]), .in4(right[5]), .in5(right[6]),
    .in6(right[7]), .in7(right[8]), .in8(right[9]), .in9(right[10]), .in10(right[11]), .in11(right[12]),
    .in12(right[13]), .in13(right[14]), .in14(1'b0), .out(result2[1]), .sel(S));  // open: in15
  Multiplexer #(.select(4)) multiplexer_18 (
    .in0(right[2]), .in1(right[3]), .in2(right[4]), .in3(right[5]), .in4(right[6]), .in5(right[7]),
    .in6(right[8]), .in7(right[9]), .in8(right[10]), .in9(right[11]), .in10(right[12]), .in11(right[13]),
    .in12(right[14]), .in13(1'b0), .in14(1'b0), .out(result2[2]), .sel(S));  // open: in15
  Multiplexer #(.select(4)) multiplexer_19 (
    .in0(right[3]), .in1(right[4]), .in2(right[5]), .in3(right[6]), .in4(right[7]), .in5(right[8]),
    .in6(right[9]), .in7(right[10]), .in8(right[11]), .in9(right[12]), .in10(right[13]), .in11(right[14]),
    .in12(1'b0), .in13(1'b0), .in14(1'b0), .out(result2[3]), .sel(S));  // open: in15
  Multiplexer #(.select(4)) multiplexer_20 (
    .in0(right[4]), .in1(right[5]), .in2(right[6]), .in3(right[7]), .in4(right[8]), .in5(right[9]),
    .in6(right[10]), .in7(right[11]), .in8(right[12]), .in9(right[13]), .in10(right[14]), .in11(1'b0),
    .in12(1'b0), .in13(1'b0), .in14(1'b0), .out(result2[4]), .sel(S));  // open: in15
  Multiplexer #(.select(4)) multiplexer_21 (
    .in0(right[5]), .in1(right[6]), .in2(right[7]), .in3(right[8]), .in4(right[9]), .in5(right[10]),
    .in6(right[11]), .in7(right[12]), .in8(right[13]), .in9(right[14]), .in10(1'b0), .in11(1'b0),
    .in12(1'b0), .in13(1'b0), .in14(1'b0), .out(result2[5]), .sel(S));  // open: in15
  Multiplexer #(.select(4)) multiplexer_22 (
    .in0(right[6]), .in1(right[7]), .in2(right[8]), .in3(right[9]), .in4(right[10]), .in5(right[11]),
    .in6(right[12]), .in7(right[13]), .in8(right[14]), .in9(1'b0), .in10(1'b0), .in11(1'b0), .in12(1'b0),
    .in13(1'b0), .in14(1'b0), .out(result2[6]), .sel(S));  // open: in15
  Multiplexer #(.select(4)) multiplexer_23 (
    .in0(right[7]), .in1(right[8]), .in2(right[9]), .in3(right[10]), .in4(right[11]), .in5(right[12]),
    .in6(right[13]), .in7(right[14]), .in8(1'b0), .in9(1'b0), .in10(1'b0), .in11(1'b0), .in12(1'b0),
    .in13(1'b0), .in14(1'b0), .out(result2[7]), .sel(S));  // open: in15
  Multiplexer #(.select(4)) multiplexer_24 (
    .in0(right[8]), .in1(right[9]), .in2(right[10]), .in3(right[11]), .in4(right[12]), .in5(right[13]),
    .in6(right[14]), .in7(1'b0), .in8(1'b0), .in9(1'b0), .in10(1'b0), .in11(1'b0), .in12(1'b0), .in13(1'b0),
    .in14(1'b0), .out(result2[8]), .sel(S));  // open: in15
  Multiplexer #(.select(4)) multiplexer_25 (
    .in0(right[9]), .in1(right[10]), .in2(right[11]), .in3(right[12]), .in4(right[13]), .in5(right[14]),
    .in6(1'b0), .in7(1'b0), .in8(1'b0), .in9(1'b0), .in10(1'b0), .in11(1'b0), .in12(1'b0), .in13(1'b0),
    .in14(1'b0), .out(result2[9]), .sel(S));  // open: in15
  Multiplexer #(.select(4)) multiplexer_26 (
    .in0(right[10]), .in1(right[11]), .in2(right[12]), .in3(right[13]), .in4(right[14]), .in5(1'b0),
    .in6(1'b0), .in7(1'b0), .in8(1'b0), .in9(1'b0), .in10(1'b0), .in11(1'b0), .in12(1'b0), .in13(1'b0),
    .in14(1'b0), .out(result2[10]), .sel(S));  // open: in15
  Multiplexer #(.select(4)) multiplexer_27 (
    .in0(right[11]), .in1(right[12]), .in2(right[13]), .in3(right[14]), .in4(1'b0), .in5(1'b0), .in6(1'b0),
    .in7(1'b0), .in8(1'b0), .in9(1'b0), .in10(1'b0), .in11(1'b0), .in12(1'b0), .in13(1'b0), .in14(1'b0),
    .out(result2[11]), .sel(S));  // open: in15
  Multiplexer #(.select(4)) multiplexer_28 (
    .in0(right[12]), .in1(right[13]), .in2(right[14]), .in3(1'b0), .in4(1'b0), .in5(1'b0), .in6(1'b0),
    .in7(1'b0), .in8(1'b0), .in9(1'b0), .in10(1'b0), .in11(1'b0), .in12(1'b0), .in13(1'b0), .in14(1'b0),
    .out(result2[12]), .sel(S));  // open: in15
  Multiplexer #(.select(4)) multiplexer_29 (
    .in0(right[13]), .in1(right[14]), .in2(1'b0), .in3(1'b0), .in4(1'b0), .in5(1'b0), .in6(1'b0), .in7(1'b0),
    .in8(1'b0), .in9(1'b0), .in10(1'b0), .in11(1'b0), .in12(1'b0), .in13(1'b0), .in14(1'b0),
    .out(result2[13]), .sel(S));  // open: in15
  Multiplexer #(.select(4)) multiplexer_30 (
    .in0(right[14]), .in1(1'b0), .in2(1'b0), .in3(1'b0), .in4(1'b0), .in5(1'b0), .in6(1'b0), .in7(1'b0),
    .in8(1'b0), .in9(1'b0), .in10(1'b0), .in11(1'b0), .in12(1'b0), .in13(1'b0), .in14(1'b0),
    .out(result2[14]), .sel(S));  // open: in15

  // Other names for the same wires on the sheet: B0 = result[0]; B1 = result[1]; B2 = result[2]; B3 = result[3];
  //   B4 = result[4]; B5 = result[5]; B6 = result[6]; B7 = result[7]; B8 = result[8]; B9 = result[9];
  //   B10 = result[10]; B11 = result[11]; B12 = result[12]; B13 = result[13]; B14 = result[14]; X0 = result2[0];
  //   X1 = result2[1]; X2 = result2[2]; X3 = result2[3]; X4 = result2[4]; X5 = result2[5]; X6 = result2[6];
  //   X7 = result2[7]; X8 = result2[8]; X9 = result2[9]; X10 = result2[10]; X11 = result2[11]; X12 = result2[12];
  //   X13 = result2[13]; X14 = result2[14]

  // Notes on the sheet:
  //   A14
  //   A13
  //   A12
  //   A11
  //   A10
  //   A9
  //   A8
  //   A7
  //   A6
  //   A5
  //   A3
  //   A4
  //   A2
  //   A1
  //   A0
  //   b14
  //   b13
  //   B12
  //   B11
  //   B10
  //   B9
  //   B8
  //   B7
  //   B6
  //   B5
  //   B4
  //   B3
  //   B2
  //   B1
  //   B0
endmodule

module adder5 (
  input  CARRY_IN,
  input  [4:0] B,
  input  [4:0] A,
  output [4:0] RSULT,
  output C_out,
  output OVERFLOW
);

  wire and_1_out, and_2_out, and_3_out, and_4_out, and_5_out, and_6_out, and_7_out, and_8_out, and_9_out,
       and_10_out, and_11_out, and_12_out, and_13_out, and_14_out, C1, C2, C3, C4, G0, G1, G2, G3, G4, P0,
       p0c0_out, P1, P2, P3, P4;

  xor xor_1 (RSULT[0], P0, CARRY_IN);
  xor xor_2 (RSULT[1], P1, C1);
  xor xor_3 (RSULT[2], P2, C2);
  xor xor_4 (RSULT[3], P3, C3);
  xor xor_5 (RSULT[4], P4, C4);
  and u_G0 (G0, A[0], B[0]);
  xor u_P0 (P0, A[0], B[0]);
  and u_G1 (G1, A[1], B[1]);
  xor u_P1 (P1, A[1], B[1]);
  and u_G2 (G2, A[2], B[2]);
  xor u_P2 (P2, A[2], B[2]);
  and u_G3 (G3, A[3], B[3]);
  xor u_P3 (P3, A[3], B[3]);
  and u_G4 (G4, A[4], B[4]);
  xor u_P4 (P4, A[4], B[4]);
  xor xor_6 (OVERFLOW, C4, C_out);
  and p0c0 (p0c0_out, CARRY_IN, P0);
  or u_C1 (C1, G0, p0c0_out);
  and and_1 (and_1_out, G0, P1);
  and and_2 (and_2_out, P1, P0, CARRY_IN);
  or u_C2 (C2, G1, and_1_out, and_2_out);
  and and_3 (and_3_out, P2, P1, G0);
  and and_4 (and_4_out, P2, P1, P0, CARRY_IN);
  and and_5 (and_5_out, P2, G1);
  and and_6 (and_6_out, G2, P3);
  and and_7 (and_7_out, G1, P2, G1);
  and and_8 (and_8_out, P3, P2, P1, G0);
  and and_9 (and_9_out, P3, P2, P1, P0, CARRY_IN);
  and and_10 (and_10_out, P4, G3);
  and and_11 (and_11_out, P4, P3, G2);
  and and_12 (and_12_out, P4, P3, P2, G1);
  and and_13 (and_13_out, P4, P3, P2, P1, G0);
  and and_14 (and_14_out, P4, P3, P2, P1, P0, CARRY_IN);
  or u_C3 (C3, G2, and_3_out, and_4_out, and_5_out);
  or u_C4 (C4, G3, and_6_out, and_7_out, and_8_out, and_9_out);
  or C5 (C_out, G4, and_10_out, and_11_out, and_12_out, and_13_out, and_14_out);

  // Other names for the same wires on the sheet: C0 = CARRY_IN; C5 = C_out
endmodule
