// Logisim project Project3Given.circ as structural Verilog: 9 circuits, main circuit CPU15
module main (
  input  EnableBreakpoint,
  input  [14:0] Breakpoint
);

  wire and_2_out, and_3_out, chipset_1_irq, CLK, clock_1_out, cpu15_1_c, cpu15_1_e, cpu15_1_i, cpu15_1_n,
       cpu15_1_o, cpu15_1_z, KBCLR, KBIRQ, KBRD, MEMCS, nand_1_out, RE, TTYCLR, TTYWE, WE;
  wire [6:0] KBDATA, TTYDATA;
  wire [7:0] cpu15_1_srf;
  wire [14:0] ADDR, chipset_1_ivect, chipset_1_led0, chipset_1_led1, chipset_1_led2, chipset_1_led3,
       chipset_1_led4, chipset_1_led5, chipset_1_led6, chipset_1_led7, chipset_1_led8, chipset_1_led9,
       chipset_1_leda, chipset_1_ledb, chipset_1_ledc, chipset_1_ledd, chipset_1_lede, cpu15_1_ib,
       cpu15_1_pc, cpu15_1_r0, cpu15_1_r1, cpu15_1_r2, cpu15_1_r3, cpu15_1_r4, cpu15_1_r5, cpu15_1_r6,
       cpu15_1_r7, cpu15_1_srp, DATA, xnor_1_out;

  Clock clock_1 (.out(clock_1_out));
  nand nand_1 (nand_1_out, EnableBreakpoint, xnor_1_out[0], xnor_1_out[1], xnor_1_out[2], xnor_1_out[3], xnor_1_out[4], xnor_1_out[5], xnor_1_out[6], xnor_1_out[7], xnor_1_out[8], xnor_1_out[9], xnor_1_out[10], xnor_1_out[11], xnor_1_out[12], xnor_1_out[13], xnor_1_out[14], 1'b1);
  and and_1 (CLK, clock_1_out, nand_1_out);
  assign xnor_1_out = ~(Breakpoint ^ cpu15_1_pc);  // XNOR_Gate xnor_1, 15 bits wide
  LED I (.in(cpu15_1_i));
  LED Z (.in(cpu15_1_z));
  LED N (.in(cpu15_1_n));
  LED O (.in(cpu15_1_o));
  LED C (.in(cpu15_1_c));
  LED E (.in(cpu15_1_e));
  and and_2 (and_2_out, WE, MEMCS);
  and and_3 (and_3_out, MEMCS, RE);
  RAM #(.addrWidth(15), .asyncread("true"), .dataWidth(15), .databus("bidir")) ram_1 (
    .addr(ADDR), .we(and_2_out), .oe(and_3_out), .clk(CLK), .data(DATA));
  // Probe on cpu15_1_pc
  // Probe on cpu15_1_ib
  // Probe on cpu15_1_srp
  // Probe on cpu15_1_srf
  // Probe on cpu15_1_r0
  // Probe on cpu15_1_r1
  // Probe on cpu15_1_r2
  // Probe on cpu15_1_r3
  // Probe on cpu15_1_r4
  // Probe on cpu15_1_r5
  // Probe on cpu15_1_r6
  // Probe on cpu15_1_r7
  CPU15 cpu15_1 (
    .I(cpu15_1_i), .Z(cpu15_1_z), .N(cpu15_1_n), .O(cpu15_1_o), .C(cpu15_1_c), .E(cpu15_1_e),
    .PC(cpu15_1_pc), .IB(cpu15_1_ib), .SRP(cpu15_1_srp), .SRF(cpu15_1_srf), .R0(cpu15_1_r0), .R1(cpu15_1_r1),
    .R2(cpu15_1_r2), .R3(cpu15_1_r3), .R4(cpu15_1_r4), .R5(cpu15_1_r5), .R6(cpu15_1_r6), .R7(cpu15_1_r7),
    .CLK(CLK), .IRQ(chipset_1_irq), .RE(RE), .WE(WE), .ADDR(ADDR), .DATAIN(DATA), .DATAOUT(DATA));
  // Probe on ADDR
  // Probe on DATA
  // Probe on chipset_1_ivect
  // Probe on TTYDATA
  CHIPSET chipset_1 (
    .RE(RE), .WE(WE), .ADDR(ADDR), .CPUDATAIN(DATA), .CPUDATAOUT(DATA), .IRQ(chipset_1_irq),
    .IVECT(chipset_1_ivect), .CLK(CLK), .MEMCS(MEMCS), .TTYWR(TTYWE), .TTYCLR(TTYCLR), .TTYDATA(TTYDATA),
    .KBRD(KBRD), .KBCLR(KBCLR), .KBIRQ(KBIRQ), .KBDATA(KBDATA), .LED0(chipset_1_led0), .LED1(chipset_1_led1),
    .LED2(chipset_1_led2), .LED3(chipset_1_led3), .LED4(chipset_1_led4), .LED5(chipset_1_led5),
    .LED6(chipset_1_led6), .LED7(chipset_1_led7), .LED8(chipset_1_led8), .LED9(chipset_1_led9),
    .LEDA(chipset_1_leda), .LEDB(chipset_1_ledb), .LEDC(chipset_1_ledc), .LEDD(chipset_1_ledd),
    .LEDE(chipset_1_lede));
  TTY tty_1 (.data(TTYDATA), .clk(CLK), .we(TTYWE), .clr(TTYCLR));
  Keyboard keyboard_1 (.clk(CLK), .re(KBRD), .clr(KBCLR), .avail(KBIRQ), .data(KBDATA));
  DotMatrix #(.matrixcols(15), .matrixrows(15)) dotmatrix_1 (
    .col0(chipset_1_led0), .col1(chipset_1_led1), .col2(chipset_1_led2), .col3(chipset_1_led3),
    .col4(chipset_1_led4), .col5(chipset_1_led5), .col6(chipset_1_led6), .col7(chipset_1_led7),
    .col8(chipset_1_led8), .col9(chipset_1_led9), .col10(chipset_1_leda), .col11(chipset_1_ledb),
    .col12(chipset_1_ledc), .col13(chipset_1_ledd), .col14(chipset_1_lede));
endmodule

// CPU
module CPU15 (
  input  [14:0] DATAIN,
  input  CLK,
  input  IRQ,
  output [14:0] PC,
  output [14:0] IB,
  output [14:0] SRP,
  output [7:0] SRF,
  output [14:0] R0,
  output [14:0] R1,
  output [14:0] R2,
  output [14:0] R3,
  output [14:0] R4,
  output [14:0] R5,
  output [14:0] R6,
  output [14:0] R7,
  output RE,
  output WE,
  output I,
  output Z,
  output [14:0] ADDR,
  output N,
  output O,
  output C,
  output E,
  output [14:0] DATAOUT
);


  // Other names for the same wires on the sheet: DATA[14:0] = DATAIN
endmodule

module CHIPSET (
  input  RE,
  input  WE,
  input  [14:0] ADDR,
  input  [14:0] CPUDATAIN,
  input  KBIRQ,
  input  [6:0] KBDATA,
  input  CLK,
  output MEMCS,
  output TTYWR,
  output [14:0] IVECT,
  output TTYCLR,
  output [6:0] TTYDATA,
  output KBRD,
  output KBCLR,
  output [14:0] CPUDATAOUT,
  output IRQ,
  output [14:0] LED0,
  output [14:0] LED1,
  output [14:0] LED2,
  output [14:0] LED3,
  output [14:0] LED4,
  output [14:0] LED5,
  output [14:0] LED6,
  output [14:0] LED7,
  output [14:0] LED8,
  output [14:0] LED9,
  output [14:0] LEDA,
  output [14:0] LEDB,
  output [14:0] LEDC,
  output [14:0] LEDD,
  output [14:0] LEDE
);

  wire and_1_out, and_8_out, and_10_out, DATA7, IOCS, IVECTADDR, IVECTEN, IVECTRE, KBCS, LED0EN, LED0END,
       LED1EN, LED1END, LED2EN, LED2END, LED3EN, LED3END, LED4EN, LED4END, LED5EN, LED5END, LED6EN, LED6END,
       LED7EN, LED7END, LED8EN, LED8END, LED9EN, LED9END, LEDAEN, LEDAEND, LEDBEN, LEDBEND, LEDCEN, LEDCEND,
       LEDCS, LEDDEN, LEDDEND, LEDEEN, LEDEEND, LEDFEND, LEDRE, multiplexer_17_out, multiplexer_18_out, RWE,
       TTYCS;
  wire [14:0] DATAL0, DATAL1, DATAL2, DATAL3, DATAL4, DATAL5, DATAL6, DATAL7, DATAL8, DATAL9, DATALA, DATALB,
       DATALC, DATALD, DATALE, LEDDATA;
  wire [14:8] KBDATA15;

  assign CPUDATAOUT = KBRD ? {KBDATA15, DATA7, KBDATA} : 15'bz;  // Controlled_Buffer controlled_buffer_1
  assign CPUDATAOUT = LEDRE ? LEDDATA : 15'bz;  // Controlled_Buffer controlled_buffer_2
  assign CPUDATAOUT = IVECTRE ? IVECT : 15'bz;  // Controlled_Buffer controlled_buffer_3
  Register #(.width(15)) register_1 (.D(DATAL0), .en(LED0EN), .Q(LED0), .clk(CLK));  // open: clr
  Register #(.width(15)) register_2 (.D(DATAL1), .en(LED1EN), .Q(LED1), .clk(CLK));  // open: clr
  Register #(.width(15)) register_3 (.D(DATAL2), .en(LED2EN), .Q(LED2), .clk(CLK));  // open: clr
  Register #(.width(15)) register_4 (.D(DATAL3), .en(LED3EN), .Q(LED3), .clk(CLK));  // open: clr
  Register #(.width(15)) register_5 (.D(DATAL4), .en(LED4EN), .Q(LED4), .clk(CLK));  // open: clr
  and and_1 (and_1_out, WE, LEDCS);
  Decoder #(.select(4)) decoder_1 (
    .out0(LED0END), .out1(LED1END), .out2(LED2END), .out3(LED3END), .out4(LED4END), .out5(LED5END),
    .out6(LED6END), .out7(LED7END), .out8(LED8END), .out9(LED9END), .out10(LEDAEND), .out11(LEDBEND),
    .out12(LEDCEND), .out13(LEDDEND), .out14(LEDEEND), .out15(LEDFEND), .sel(ADDR[3:0]), .en(and_1_out));
  Register #(.width(15)) register_6 (.D(DATAL5), .en(LED5EN), .Q(LED5), .clk(CLK));  // open: clr
  Register #(.width(15)) register_7 (.D(DATAL6), .en(LED6EN), .Q(LED6), .clk(CLK));  // open: clr
  Register #(.width(15)) register_8 (.D(DATAL7), .en(LED7EN), .Q(LED7), .clk(CLK));  // open: clr
  Register #(.width(15)) register_9 (.D(DATAL8), .en(LED8EN), .Q(LED8), .clk(CLK));  // open: clr
  Register #(.width(15)) register_10 (.D(DATAL9), .en(LED9EN), .Q(LED9), .clk(CLK));  // open: clr
  or or_1 (LED0EN, LED0END, LEDFEND);
  or or_2 (LED1EN, LED1END, LEDFEND);
  or or_3 (LED2EN, LED2END, LEDFEND);
  or or_4 (LED3EN, LED3END, LEDFEND);
  or or_5 (LED4EN, LED4END, LEDFEND);
  or or_6 (LED5EN, LED5END, LEDFEND);
  or or_7 (LED6EN, LED6END, LEDFEND);
  or or_8 (LED7EN, LED7END, LEDFEND);
  or or_9 (LED8EN, LED8END, LEDFEND);
  or or_10 (LED9EN, LED9END, LEDFEND);
  or or_11 (LEDAEN, LEDAEND, LEDFEND);
  or or_12 (LEDBEN, LEDBEND, LEDFEND);
  or or_13 (LEDCEN, LEDCEND, LEDFEND);
  or or_14 (LEDDEN, LEDDEND, LEDFEND);
  or or_15 (LEDEEN, LEDEEND, LEDFEND);
  Pull_Resistor pull_resistor_1 (.node(KBDATA15[14]));
  Pull_Resistor pull_resistor_2 (.node(KBDATA15[13]));
  Pull_Resistor pull_resistor_3 (.node(KBDATA15[12]));
  Pull_Resistor pull_resistor_4 (.node(KBDATA15[11]));
  Pull_Resistor pull_resistor_5 (.node(KBDATA15[10]));
  Pull_Resistor pull_resistor_6 (.node(KBDATA15[9]));
  Pull_Resistor pull_resistor_7 (.node(KBDATA15[8]));
  Pull_Resistor pull_resistor_8 (.node(DATA7));
  Register #(.width(15)) register_11 (.D(DATALA), .en(LEDAEN), .Q(LEDA), .clk(CLK));  // open: clr
  Register #(.width(15)) register_12 (.D(DATALB), .en(LEDBEN), .Q(LEDB), .clk(CLK));  // open: clr
  Register #(.width(15)) register_13 (.D(DATALC), .en(LEDCEN), .Q(LEDC), .clk(CLK));  // open: clr
  Register #(.width(15)) register_14 (.D(DATALD), .en(LEDDEN), .Q(LEDD), .clk(CLK));  // open: clr
  Register #(.width(15)) register_15 (.D(DATALE), .en(LEDEEN), .Q(LEDE), .clk(CLK));  // open: clr
  Multiplexer #(.width(15)) multiplexer_1 (.in0(CPUDATAIN), .in1(LED1), .out(DATAL0), .sel(LEDFEND));
  Multiplexer #(.width(15)) multiplexer_2 (.in0(CPUDATAIN), .in1(LED2), .out(DATAL1), .sel(LEDFEND));
  Multiplexer #(.width(15)) multiplexer_3 (.in0(CPUDATAIN), .in1(LED3), .out(DATAL2), .sel(LEDFEND));
  Multiplexer #(.width(15)) multiplexer_4 (.in0(CPUDATAIN), .in1(LED4), .out(DATAL3), .sel(LEDFEND));
  Multiplexer #(.width(15)) multiplexer_5 (.in0(CPUDATAIN), .in1(LED5), .out(DATAL4), .sel(LEDFEND));
  Multiplexer #(.select(4), .width(15)) multiplexer_6 (
    .in0(LED0), .in1(LED1), .in2(LED2), .in3(LED3), .in4(LED4), .in5(LED5), .in6(LED6), .in7(LED7),
    .in8(LED8), .in9(LED9), .in10(LEDA), .in11(LEDB), .in12(LEDC), .in13(LEDD), .in14(LEDE),
    .in15({15{1'b0}}), .out(LEDDATA), .sel(ADDR[3:0]));
  Multiplexer #(.width(15)) multiplexer_7 (.in0(CPUDATAIN), .in1(LED6), .out(DATAL5), .sel(LEDFEND));
  Multiplexer #(.width(15)) multiplexer_8 (.in0(CPUDATAIN), .in1(LED7), .out(DATAL6), .sel(LEDFEND));
  Multiplexer #(.width(15)) multiplexer_9 (.in0(CPUDATAIN), .in1(LED8), .out(DATAL7), .sel(LEDFEND));
  Multiplexer #(.width(15)) multiplexer_10 (.in0(CPUDATAIN), .in1(LED9), .out(DATAL8), .sel(LEDFEND));
  Multiplexer #(.width(15)) multiplexer_11 (.in0(CPUDATAIN), .in1(LEDA), .out(DATAL9), .sel(LEDFEND));
  and and_2 (LEDRE, RE, LEDCS);
  Multiplexer #(.width(15)) multiplexer_12 (.in0(CPUDATAIN), .in1(LEDB), .out(DATALA), .sel(LEDFEND));
  Multiplexer #(.width(15)) multiplexer_13 (.in0(CPUDATAIN), .in1(LEDC), .out(DATALB), .sel(LEDFEND));
  Multiplexer #(.width(15)) multiplexer_14 (.in0(CPUDATAIN), .in1(LEDD), .out(DATALC), .sel(LEDFEND));
  Multiplexer #(.width(15)) multiplexer_15 (.in0(CPUDATAIN), .in1(LEDE), .out(DATALD), .sel(LEDFEND));
  Multiplexer #(.width(15)) multiplexer_16 (.in0(CPUDATAIN), .in1(CPUDATAIN), .out(DATALE), .sel(LEDFEND));
  and and_3 (IOCS, ADDR[5], ADDR[6], ADDR[7], ADDR[8], ADDR[9], ADDR[10], ADDR[11], ADDR[12], ADDR[13], ADDR[14], 1'b1);
  and and_4 (TTYCS, IOCS, ADDR[0], ~ADDR[1], ~ADDR[2], ~ADDR[3], ADDR[4]);  // AND_Gate
  and and_5 (KBCS, IOCS, ~ADDR[0], ~ADDR[1], ~ADDR[2], ~ADDR[3], ADDR[4]);  // AND_Gate
  and and_6 (IVECTADDR, ADDR[0], ADDR[1], ADDR[2], ADDR[3], ADDR[4], ADDR[5], ADDR[6], ADDR[7], ADDR[8], ADDR[9], ADDR[10], ADDR[11], ADDR[12], ADDR[13], ADDR[14]);
  and and_7 (TTYWR, TTYCS, WE);
  and and_8 (and_8_out, TTYWR, DATA7);
  and and_9 (KBRD, KBCS, RE);
  and and_10 (and_10_out, KBCS, WE);
  Multiplexer multiplexer_17 (.in0(and_10_out), .in1(1'b0), .out(multiplexer_17_out), .sel(KBCLR));
  and and_11 (LEDCS, IOCS, ~ADDR[4], RWE);  // AND_Gate
  and and_12 (IVECTEN, IVECTADDR, WE);
  and and_13 (IVECTRE, IVECTADDR, RE);
  or or_16 (RWE, RE, WE);
  and and_14 (MEMCS, ~IOCS, RWE);  // AND_Gate
  Multiplexer multiplexer_18 (.in0(and_8_out), .in1(1'b0), .out(multiplexer_18_out), .sel(TTYCLR));
  D_Flip_Flop d_ff_1 (.clk(CLK), .D(multiplexer_17_out), .Q(KBCLR));  // open: Qn, preset, reset
  Register #(.width(15)) register_16 (.D(CPUDATAIN), .en(IVECTEN), .Q(IVECT), .clk(CLK));  // open: clr
  D_Flip_Flop d_ff_2 (.clk(CLK), .D(multiplexer_18_out), .Q(TTYCLR));  // open: Qn, preset, reset

  assign IRQ = KBIRQ;
  assign TTYDATA = CPUDATAIN[6:0];

  // Other names for the same wires on the sheet: DATA[14:0] = CPUDATAIN; KBDATA15[7:0] = {DATA7, KBDATA}
endmodule

module ADDER15 (
  input  [14:0] A,
  input  [14:0] B,
  input  CIN,
  output COUT,
  output [14:0] S
);

  wire and_11_out, and_12_out, and_13_out, and_14_out, and_15_out, and_16_out, and_17_out, and_18_out,
       and_19_out, and_20_out, and_21_out, and_22_out, and_23_out, and_24_out, and_25_out, and_26_out,
       and_27_out, and_28_out, and_29_out, and_30_out, and_31_out, and_32_out, and_33_out, and_34_out,
       and_35_out, and_36_out, and_37_out, and_38_out, and_39_out, and_40_out, and_41_out, and_42_out,
       and_43_out, and_44_out, and_45_out, and_46_out, and_47_out, and_48_out, and_49_out, and_50_out,
       and_51_out, and_52_out, and_53_out, and_54_out, C1, C1X, C1Y, C2, C2X, C2Y, C3, C3X, C3Y, C4, C4X,
       C4Y, C5, C5X, G0, G0X, G0Y, G1, G1X, G1Y, G2, G2X, G2Y, G3, G3X, G3Y, G4, G4X, G4Y, P0, p0c0_out, P0X,
       P0Y, P1, P1X, P1Y, P2, P2X, P2Y, P3, P3X, P3Y, P4, P4X, P4Y;

  xor xor_1 (S[0], P0, CIN);
  xor xor_2 (S[1], P1, C1);
  xor xor_3 (S[2], P2, C2);
  xor xor_4 (S[3], P3, C3);
  xor xor_5 (S[4], P4, C4);
  and and_1 (G0X, A[5], B[5]);
  xor xor_6 (P0X, A[5], B[5]);
  and and_2 (G1X, A[6], B[6]);
  xor xor_7 (P1X, A[6], B[6]);
  and and_3 (G2X, A[7], B[7]);
  xor xor_8 (P2X, A[7], B[7]);
  and and_4 (G3X, A[8], B[8]);
  xor xor_9 (P3X, A[8], B[8]);
  and and_5 (G4X, A[9], B[9]);
  xor xor_10 (P4X, A[9], B[9]);
  and u_G0 (G0, A[0], B[0]);
  xor u_P0 (P0, A[0], B[0]);
  and u_G1 (G1, A[1], B[1]);
  xor u_P1 (P1, A[1], B[1]);
  and u_G2 (G2, A[2], B[2]);
  xor u_P2 (P2, A[2], B[2]);
  and u_G3 (G3, A[3], B[3]);
  xor u_P3 (P3, A[3], B[3]);
  and u_G4 (G4, A[4], B[4]);
  xor u_P4 (P4, A[4], B[4]);
  and and_6 (G0Y, A[10], B[10]);
  xor xor_11 (P0Y, A[10], B[10]);
  and and_7 (G1Y, A[11], B[11]);
  xor xor_12 (P1Y, A[11], B[11]);
  and and_8 (G2Y, A[12], B[12]);
  xor xor_13 (P2Y, A[12], B[12]);
  and and_9 (G3Y, A[13], B[13]);
  xor xor_14 (P3Y, A[13], B[13]);
  and and_10 (G4Y, A[14], B[14]);
  xor xor_15 (P4Y, A[14], B[14]);
  and and_11 (and_11_out, C5, P0X);
  and p0c0 (p0c0_out, CIN, P0);
  or or_1 (C1X, G0X, and_11_out);
  and and_12 (and_12_out, G0X, P1X);
  and and_13 (and_13_out, P1X, P0X, C5);
  and and_14 (and_14_out, C5X, P0Y);
  xor xor_16 (S[6], P1X, C1X);
  xor xor_17 (S[8], P3X, C3X);
  xor xor_18 (S[9], P4X, C4X);
  or u_C1 (C1, G0, p0c0_out);
  and and_15 (and_15_out, G0, P1);
  and and_16 (and_16_out, P1, P0, CIN);
  or or_2 (C1Y, G0Y, and_14_out);
  and and_17 (and_17_out, G0Y, P1Y);
  and and_18 (and_18_out, P1Y, P0Y, C5X);
  xor xor_19 (S[5], P0X, C5);
  xor xor_20 (S[7], P2X, C2X);
  or or_3 (C2X, G1X, and_12_out, and_13_out);
  or u_C2 (C2, G1, and_15_out, and_16_out);
  or or_4 (C2Y, G1Y, and_17_out, and_18_out);
  xor xor_21 (S[10], P0Y, C5X);
  xor xor_22 (S[11], P1Y, C1Y);
  xor xor_23 (S[12], P2Y, C2Y);
  xor xor_24 (S[13], P3Y, C3Y);
  xor xor_25 (S[14], P4Y, C4Y);
  and and_19 (and_19_out, P2X, P1X, G0X);
  and and_20 (and_20_out, P2X, P1X, P0X, C5);
  and and_21 (and_21_out, P2X, G1X);
  and and_22 (and_22_out, G2X, P3X);
  and and_23 (and_23_out, G1X, P2X, G1X);
  and and_24 (and_24_out, P3X, P2X, P1X, G0X);
  and and_25 (and_25_out, P3X, P2X, P1X, P0X, C5);
  and and_26 (and_26_out, P4X, G3X);
  and and_27 (and_27_out, P4X, P3X, G2X);
  and and_28 (and_28_out, P4X, P3X, P2X, G1X);
  and and_29 (and_29_out, P4X, P3X, P2X, P1X, G0X);
  and and_30 (and_30_out, P4X, P3X, P2X, P1X, P0X, C5);
  and and_31 (and_31_out, P4Y, G3Y);
  and and_32 (and_32_out, P4Y, P3Y, G2Y);
  and and_33 (and_33_out, P2, P1, G0);
  and and_34 (and_34_out, P2, P1, P0, CIN);
  and and_35 (and_35_out, P2, G1);
  and and_36 (and_36_out, G2, P3);
  and and_37 (and_37_out, G1, P2, G1);
  and and_38 (and_38_out, P3, P2, P1, G0);
  and and_39 (and_39_out, P3, P2, P1, P0, CIN);
  and and_40 (and_40_out, P4, G3);
  and and_41 (and_41_out, P4, P3, G2);
  and and_42 (and_42_out, P4, P3, P2, G1);
  and and_43 (and_43_out, P4, P3, P2, P1, G0);
  and and_44 (and_44_out, P4, P3, P2, P1, P0, CIN);
  and and_45 (and_45_out, P2Y, P1Y, G0Y);
  and and_46 (and_46_out, P2Y, P1Y, P0Y, C5X);
  and and_47 (and_47_out, P2Y, G1Y);
  and and_48 (and_48_out, G2Y, P3Y);
  and and_49 (and_49_out, G1Y, P2Y, G1Y);
  and and_50 (and_50_out, P3Y, P2Y, P1Y, G0Y);
  and and_51 (and_51_out, P3Y, P2Y, P1Y, P0Y, C5X);
  and and_52 (and_52_out, P4Y, P3Y, P2Y, G1Y);
  and and_53 (and_53_out, P4Y, P3Y, P2Y, P1Y, G0Y);
  and and_54 (and_54_out, P4Y, P3Y, P2Y, P1Y, P0Y, C5X);
  or or_5 (C3X, G2X, and_19_out, and_20_out, and_21_out);
  or u_C3 (C3, G2, and_33_out, and_34_out, and_35_out);
  or or_6 (C4X, G3X, and_22_out, and_23_out, and_24_out, and_25_out);
  or or_7 (C3Y, G2Y, and_45_out, and_46_out, and_47_out);
  or u_C4 (C4, G3, and_36_out, and_37_out, and_38_out, and_39_out);
  or or_8 (C5X, G4X, and_26_out, and_27_out, and_28_out, and_29_out, and_30_out);
  or or_9 (C4Y, G3Y, and_48_out, and_49_out, and_50_out, and_51_out);
  or or_10 (COUT, G4Y, and_31_out, and_32_out, and_52_out, and_53_out, and_54_out);
  or u_C5 (C5, G4, and_40_out, and_41_out, and_42_out, and_43_out, and_44_out);

  // Other names for the same wires on the sheet: A1[4:0] = A[4:0]; A2[4:0] = A[9:5]; A3[4:0] = A[14:10];
  //   B1[4:0] = B[4:0]; B2[4:0] = B[9:5]; B3[4:0] = B[14:10]; C5Y = COUT; S1[4:0] = S[4:0]; S2[4:0] = S[9:5];
  //   S3[4:0] = S[14:10]
endmodule

module REGS15 (
  input  [14:0] D,
  input  W,
  input  [2:0] SelD,
  input  CLK,
  input  [2:0] SelA,
  input  [2:0] SelB,
  output [14:0] R0,
  output [14:0] R1,
  output [14:0] R2,
  output [14:0] R3,
  output [14:0] R4,
  output [14:0] R5,
  output [14:0] R6,
  output [14:0] R7,
  output [14:0] A,
  output [14:0] B
);

  wire W_1, W_2, W_3, W_4, W_5, W_6, W_7;

  Register #(.width(15)) register_1 (.D({15{1'b0}}), .clk(CLK), .Q(R0));  // open: en, clr
  Decoder #(.select(3)) decoder_1 (
    .out1(W_1), .out2(W_2), .out3(W_3), .out4(W_4), .out5(W_5), .out6(W_6), .out7(W_7), .sel(SelD), .en(W));  // open: out0
  Multiplexer #(.select(3), .width(15)) multiplexer_1 (
    .in0(R0), .in1(R1), .in2(R2), .in3(R3), .in4(R4), .in5(R5), .in6(R6), .in7(R7), .out(A), .sel(SelA));
  Register #(.width(15)) register_2 (.D(D), .en(W_1), .clk(CLK), .Q(R1));  // open: clr
  Register #(.width(15)) register_3 (.D(D), .en(W_2), .clk(CLK), .Q(R2));  // open: clr
  Register #(.width(15)) register_4 (.D(D), .en(W_3), .clk(CLK), .Q(R3));  // open: clr
  Multiplexer #(.select(3), .width(15)) multiplexer_2 (
    .in0(R0), .in1(R1), .in2(R2), .in3(R3), .in4(R4), .in5(R5), .in6(R6), .in7(R7), .out(B), .sel(SelB));
  Register #(.width(15)) register_5 (.D(D), .en(W_4), .clk(CLK), .Q(R4));  // open: clr
  Register #(.width(15)) register_6 (.D(D), .en(W_5), .clk(CLK), .Q(R5));  // open: clr
  Register #(.width(15)) register_7 (.D(D), .en(W_6), .clk(CLK), .Q(R6));  // open: clr
  Register #(.width(15)) register_8 (.D(D), .en(W_7), .clk(CLK), .Q(R7));  // open: clr
endmodule

module ALU15 (
  input  [14:0] A,
  input  [14:0] B,
  input  [2:0] OP,
  input  CIN,
  input  OIN,
  output C,
  output O,
  output N,
  output Z,
  output [14:0] R
);
endmodule

module FLAGS8 (
  input  IRQ,
  input  [7:0] NF,
  input  [7:0] WM,
  input  CLK,
  output [7:0] F
);
endmodule

module IMM15 (
  input  [14:0] INST,
  output [14:0] SEXT
);

  wire and_1_out, and_2_out, and_3_out, and_4_out, and_6_out, and_7_out, Encode_0_a, Encode_0_b, Encode_0_c,
       Encode_1_a, Encode_2_a, not_6_out, not_7_out, NOT_OP_0, NOT_OP_1, NOT_OP_2, NOT_OP_3, NOT_OP_4;
  wire [2:0] or_5_out;

  and and_1 (and_1_out, INST[3], NOT_OP_4);
  and and_2 (and_2_out, INST[0], INST[1], NOT_OP_2, INST[3], INST[4]);
  and and_3 (and_3_out, INST[4], INST[3], INST[2], NOT_OP_1, NOT_OP_0);
  and and_4 (and_4_out, INST[4], INST[3], INST[2], NOT_OP_1, INST[0]);
  and and_5 (Encode_0_c, INST[4], INST[3], INST[2], INST[1], INST[0]);
  or or_1 (Encode_0_b, and_3_out, and_4_out);
  LED Bits_11 (.in(Encode_0_c));
  not not_1 (NOT_OP_0, INST[0]);
  not not_2 (NOT_OP_1, INST[1]);
  not not_3 (NOT_OP_2, INST[2]);
  not not_4 (NOT_OP_3, INST[3]);
  not not_5 (NOT_OP_4, INST[4]);
  or or_2 (Encode_0_a, and_1_out, and_2_out);
  LED Bits_4 (.in(Encode_0_a));
  LED Bits_7 (.in(Encode_0_b));
  Register #(.trigger("high"), .width(15)) register_1 (.D(SEXT), .en(1'b1), .clk(1'b1));  // open: Q, clr
  and and_6 (and_6_out, INST[2], INST[1], NOT_OP_0);
  and and_7 (and_7_out, INST[2], INST[1], INST[0]);
  or or_3 (or_5_out[2], Encode_0_c, Encode_2_a);
  not not_6 (not_6_out, and_6_out);
  not not_7 (not_7_out, and_7_out);
  or or_4 (or_5_out[1], Encode_0_b, Encode_1_a);
  and and_8 (Encode_1_a, INST[4], NOT_OP_3, not_6_out, not_7_out);
  and and_9 (Encode_2_a, INST[4], INST[3], INST[2], INST[1], NOT_OP_0);
  Multiplexer #(.select(3), .width(15)) multiplexer_1 (
    .in0({15{1'b0}}), .in1({{12{INST[14]}}, INST[13:11]}), .in2({{6{INST[14]}}, INST[13:5]}),
    .in3({{9{INST[14]}}, INST[13:8]}), .in4({{12{INST[14]}}, INST[7:5]}),
    .in5({{5{INST[14]}}, INST[13:8], 4'b0000}), .in6({15{1'b0}}), .in7({15{1'b0}}), .out(SEXT), .sel(or_5_out));
  LED Bits_10 (.in(Encode_1_a));
  or or_5 (or_5_out[0], Encode_0_c, Encode_0_b, Encode_0_a);
  LED Bits_4_SW (.in(Encode_2_a));

  // Other names for the same wires on the sheet: Bits_4_SW[14:0] = {{12{INST[14]}}, INST[7:5]};
  //   Bits_10[14:0] = {{6{INST[14]}}, INST[13:5]}; Bits_4[14:0] = {{12{INST[14]}}, INST[13:11]};
  //   Bits_7[14:0] = {{9{INST[14]}}, INST[13:8]}; Bits_11[14:4] = {{5{INST[14]}}, INST[13:8]};
  //   Encode_1_b = Encode_0_b; Encode_2_b = Encode_0_c; OP_0 = INST[0]; OP_1 = INST[1]; OP_2 = INST[2];
  //   OP_3 = INST[3]; OP_4 = INST[4]
endmodule

module DECODE15 (
  input  [4:0] OPCODE,
  output SWI,
  output STORE,
  output LOAD,
  output [1:0] ASEL,
  output [1:0] BSEL,
  output [2:0] ALUOP,
  output [2:0] REGDATASRC,
  output REGW,
  output [1:0] FLAGSRC,
  output [7:0] FLAGWM,
  output SRPW,
  output SRFW
);
endmodule
